// Logisim project 24.10.circ as structural Verilog: 53 circuits, main circuit Ha
module Ha (
  input  A,
  input  B,
  output Cout,
  output S
);

  and and_1 (Cout, A, B);
  xor xor_1 (S, A, B);
endmodule

module teste (
  input  SUB,
  input  in_2,
  input  in_3,
  input  in_4,
  input  in_5,
  input  in_6,
  input  in_7,
  input  in_8,
  input  in_9,
  output out_10,
  output out_11,
  output out_12,
  output out_13,
  output out_14
);

  wire fa_1_cout, fa_2_cout, fa_3_cout, xor_1_out, xor_2_out, xor_3_out, xor_4_out;

  xor xor_1 (xor_1_out, SUB, in_7);
  FA fa_1 (.A(in_2), .B(xor_1_out), .Cin(SUB), .Cout(fa_1_cout), .S(out_10));
  xor xor_2 (xor_2_out, SUB, in_8);
  xor xor_3 (xor_3_out, SUB, in_9);
  FA fa_2 (.A(in_3), .B(xor_2_out), .Cin(fa_1_cout), .Cout(fa_2_cout), .S(out_11));
  FA fa_3 (.A(in_4), .B(xor_3_out), .Cin(fa_2_cout), .Cout(fa_3_cout), .S(out_12));
  xor xor_4 (xor_4_out, SUB, in_6);
  FA fa_4 (.A(in_5), .B(xor_4_out), .Cin(fa_3_cout), .Cout(out_14), .S(out_13));
endmodule

module FA (
  input  A,
  input  B,
  input  Cin,
  output Cout,
  output S
);

  wire and_1_out, and_2_out, and_3_out;

  and and_1 (and_1_out, A, B);
  and and_2 (and_2_out, B, Cin);
  and and_3 (and_3_out, A, Cin);
  xor odd_parity_1 (S, A, B, Cin);
  or or_1 (Cout, and_1_out, and_2_out, and_3_out);
endmodule

module multiplicador_5bits (
  input  in_1,
  input  in_2,
  input  in_3,
  input  in_4,
  input  in_5,
  input  in_6,
  input  in_7,
  input  in_8,
  input  in_9,
  input  in_10,
  output out_11,
  output out_12,
  output out_13,
  output out_14,
  output out_15,
  output out_16,
  output out_17,
  output out_18,
  output out_19,
  output out_20
);

  wire A0B1_out, A0B2_out, A0B3_out, A0B4_out, A1B0_out, A1B1_out, A1B2_out, A1B3_out, A1B4_out, A2B0_out,
       A2B1_out, A2B2_out, A2B3_out, A2B4_out, A3B0_out, A3B1_out, A3B2_out, A3B3_out, A3B4_out, A4B0_out,
       A4B1_out, A4B2_out, A4B3_out, A4B4_out, fa_1_cout, fa_1_s, fa_2_cout, fa_2_s, fa_3_cout, fa_3_s,
       fa_4_cout, fa_4_s, fa_5_cout, fa_5_s, fa_6_cout, fa_7_cout, fa_7_s, fa_8_cout, fa_8_s, fa_9_cout,
       fa_10_cout, fa_10_s, fa_11_cout, fa_11_s, fa_12_cout, fa_13_cout, fa_13_s, fa_14_cout, ha_1_cout,
       ha_2_cout, ha_3_cout, ha_4_cout, ha_4_s, ha_5_cout, ha_5_s;

  and A0B0 (out_20, in_5, in_10);
  and A1B0 (A1B0_out, in_4, in_10);
  and A0B1 (A0B1_out, in_5, in_9);
  Ha ha_1 (.A(A0B1_out), .B(A1B0_out), .Cout(ha_1_cout), .S(out_19));
  FA fa_1 (.A(A2B0_out), .B(A1B1_out), .Cin(ha_1_cout), .Cout(fa_1_cout), .S(fa_1_s));
  and A2B0 (A2B0_out, in_3, in_10);
  and A1B1 (A1B1_out, in_4, in_9);
  and A0B2 (A0B2_out, in_5, in_8);
  Ha ha_2 (.A(A0B2_out), .B(fa_1_s), .Cout(ha_2_cout), .S(out_18));
  and A3B0 (A3B0_out, in_2, in_10);
  and A2B1 (A2B1_out, in_3, in_9);
  and A1B2 (A1B2_out, in_4, in_8);
  and A0B3 (A0B3_out, in_5, in_7);
  FA fa_2 (.A(A0B3_out), .B(fa_1_cout), .Cin(ha_2_cout), .Cout(fa_2_cout), .S(fa_2_s));
  FA fa_3 (.A(A3B0_out), .B(A2B1_out), .Cin(A1B2_out), .Cout(fa_3_cout), .S(fa_3_s));
  Ha ha_3 (.A(fa_3_s), .B(fa_2_s), .Cout(ha_3_cout), .S(out_17));
  and A4B0 (A4B0_out, in_1, in_10);
  and A3B1 (A3B1_out, in_2, in_9);
  and A2B2 (A2B2_out, in_3, in_8);
  and A1B3 (A1B3_out, in_4, in_7);
  and A0B4 (A0B4_out, in_5, in_6);
  FA fa_4 (.A(fa_3_cout), .B(ha_3_cout), .Cin(fa_2_cout), .Cout(fa_4_cout), .S(fa_4_s));
  Ha ha_4 (.A(A4B0_out), .B(A3B1_out), .Cout(ha_4_cout), .S(ha_4_s));
  FA fa_5 (.A(A2B2_out), .B(A1B3_out), .Cin(A0B4_out), .Cout(fa_5_cout), .S(fa_5_s));
  FA fa_6 (.A(ha_4_s), .B(fa_5_s), .Cin(fa_4_s), .Cout(fa_6_cout), .S(out_16));
  and A4B1 (A4B1_out, in_1, in_9);
  and A3B2 (A3B2_out, in_2, in_8);
  and A2B3 (A2B3_out, in_3, in_7);
  and A1B4 (A1B4_out, in_4, in_6);
  FA fa_7 (.A(A3B2_out), .B(A2B3_out), .Cin(A1B4_out), .Cout(fa_7_cout), .S(fa_7_s));
  FA fa_8 (.A(ha_4_cout), .B(fa_5_cout), .Cin(fa_6_cout), .Cout(fa_8_cout), .S(fa_8_s));
  Ha ha_5 (.A(A4B1_out), .B(fa_4_cout), .Cout(ha_5_cout), .S(ha_5_s));
  FA fa_9 (.A(fa_7_s), .B(ha_5_s), .Cin(fa_8_s), .Cout(fa_9_cout), .S(out_15));
  and A4B2 (A4B2_out, in_1, in_8);
  and A3B3 (A3B3_out, in_2, in_7);
  and A2B4 (A2B4_out, in_3, in_6);
  FA fa_10 (.A(fa_7_cout), .B(fa_8_cout), .Cin(ha_5_cout), .Cout(fa_10_cout), .S(fa_10_s));
  FA fa_11 (.A(A4B2_out), .B(A3B3_out), .Cin(A2B4_out), .Cout(fa_11_cout), .S(fa_11_s));
  FA fa_12 (.A(fa_10_s), .B(fa_9_cout), .Cin(fa_11_s), .Cout(fa_12_cout), .S(out_14));
  and A4B3 (A4B3_out, in_1, in_7);
  and A3B4 (A3B4_out, in_2, in_6);
  FA fa_13 (.A(fa_11_cout), .B(fa_10_cout), .Cin(fa_12_cout), .Cout(fa_13_cout), .S(fa_13_s));
  FA fa_14 (.A(A4B3_out), .B(A3B4_out), .Cin(fa_13_s), .Cout(fa_14_cout), .S(out_13));
  and A4B4 (A4B4_out, in_1, in_6);
  FA fa_15 (.A(A4B4_out), .B(fa_14_cout), .Cin(fa_13_cout), .Cout(out_11), .S(out_12));

  // Other names for the same wires on the sheet: A0 = in_5; A1 = in_4; A2 = in_3; A3 = in_2; A4 = in_1; B0 = in_10;
  //   B1 = in_9; B2 = in_8; B3 = in_7; B4 = in_6; S0 = out_20; S1 = out_19; S2 = out_18; S3 = out_17; S4 = out_16;
  //   S5 = out_15; S6 = out_14; S7 = out_13; S8 = out_12; S9 = out_11
endmodule

module mult2bits (
  input  in_1,
  input  in_2,
  input  in_3,
  input  in_4,
  output out_5,
  output out_6,
  output out_7,
  output out_8
);

  wire and_2_out, and_3_out, and_4_out, ha_1_cout;

  and and_1 (out_8, in_2, in_4);
  and and_2 (and_2_out, in_1, in_4);
  and and_3 (and_3_out, in_2, in_3);
  and and_4 (and_4_out, in_1, in_3);
  Ha ha_1 (.A(and_2_out), .B(and_3_out), .Cout(ha_1_cout), .S(out_7));
  Ha ha_2 (.A(ha_1_cout), .B(and_4_out), .Cout(out_5), .S(out_6));

  // Other names for the same wires on the sheet: A0 = in_2; A1 = in_1; B0 = in_4; B1 = in_3; S0 = out_8; S1 = out_7;
  //   S2 = out_6; S3 = out_5
endmodule

module mult4bits (
  input  in_1,
  input  in_2,
  input  in_3,
  input  in_4,
  input  in_5,
  input  in_6,
  input  in_7,
  input  in_8,
  output out_9,
  output out_10,
  output out_11,
  output out_12,
  output out_13,
  output out_14,
  output out_15,
  output out_16
);

  wire and_2_out, and_3_out, and_4_out, and_5_out, and_6_out, and_7_out, and_8_out, and_9_out, and_10_out,
       and_11_out, and_12_out, and_13_out, and_14_out, and_15_out, and_16_out, fa_1_cout, fa_1_s, fa_2_cout,
       fa_2_s, fa_3_cout, fa_3_s, fa_4_cout, fa_4_s, fa_5_cout, fa_5_s, fa_6_cout, fa_7_cout, fa_7_s,
       ha_1_cout, ha_2_cout, ha_3_cout, ha_4_cout;

  and and_1 (out_16, in_4, in_8);
  and and_2 (and_2_out, in_3, in_8);
  and and_3 (and_3_out, in_4, in_7);
  and and_4 (and_4_out, in_1, in_7);
  and and_5 (and_5_out, in_2, in_8);
  Ha ha_1 (.A(and_2_out), .B(and_3_out), .Cout(ha_1_cout), .S(out_15));
  FA fa_1 (.A(and_4_out), .B(and_7_out), .Cin(and_6_out), .Cout(fa_1_cout), .S(fa_1_s));
  and and_6 (and_6_out, in_2, in_6);
  and and_7 (and_7_out, in_3, in_5);
  and and_8 (and_8_out, in_3, in_7);
  FA fa_2 (.A(and_8_out), .B(and_5_out), .Cin(ha_1_cout), .Cout(fa_2_cout), .S(fa_2_s));
  Ha ha_2 (.A(fa_2_s), .B(and_9_out), .Cout(ha_2_cout), .S(out_14));
  FA fa_3 (.A(fa_7_cout), .B(fa_5_cout), .Cin(ha_4_cout), .Cout(fa_3_cout), .S(fa_3_s));
  Ha ha_3 (.A(fa_3_s), .B(fa_1_s), .Cout(ha_3_cout), .S(out_12));
  and and_9 (and_9_out, in_4, in_6);
  FA fa_4 (.A(fa_3_cout), .B(ha_3_cout), .Cin(fa_1_cout), .Cout(fa_4_cout), .S(fa_4_s));
  and and_10 (and_10_out, in_2, in_5);
  and and_11 (and_11_out, in_2, in_7);
  and and_12 (and_12_out, in_1, in_8);
  FA fa_5 (.A(and_12_out), .B(fa_2_cout), .Cin(ha_2_cout), .Cout(fa_5_cout), .S(fa_5_s));
  Ha ha_4 (.A(fa_7_s), .B(fa_5_s), .Cout(ha_4_cout), .S(out_13));
  and and_13 (and_13_out, in_1, in_6);
  and and_14 (and_14_out, in_3, in_6);
  and and_15 (and_15_out, in_1, in_5);
  FA fa_6 (.A(fa_4_s), .B(and_10_out), .Cin(and_13_out), .Cout(fa_6_cout), .S(out_11));
  and and_16 (and_16_out, in_4, in_5);
  FA fa_7 (.A(and_16_out), .B(and_14_out), .Cin(and_11_out), .Cout(fa_7_cout), .S(fa_7_s));
  FA fa_8 (.A(fa_4_cout), .B(fa_6_cout), .Cin(and_15_out), .Cout(out_9), .S(out_10));

  // Other names for the same wires on the sheet: A0 = in_4; A1 = in_3; A2 = in_2; A3 = in_1; B0 = in_8; B1 = in_7;
  //   B2 = in_6; B3 = in_5; S0 = out_16; S1 = out_15; S2 = out_14; S3 = out_13; S4 = out_12; S5 = out_11; S6 = out_10;
  //   S7 = out_9
endmodule

module Multiplexador (
  input  A,
  input  B,
  input  C,
  input  D,
  input  SEL_1,
  input  SEL_0,
  output S
);

  wire and_1_out, and_2_out, and_3_out, and_4_out, not_1_out, not_2_out, not_3_out, not_4_out;

  not not_1 (not_1_out, SEL_1);
  not not_2 (not_2_out, SEL_0);
  not not_3 (not_3_out, SEL_1);
  not not_4 (not_4_out, SEL_0);
  and and_1 (and_1_out, not_1_out, not_2_out, A);
  and and_2 (and_2_out, not_3_out, SEL_0, B);
  and and_3 (and_3_out, SEL_1, not_4_out, C);
  and and_4 (and_4_out, SEL_1, SEL_0, D);
  or or_1 (S, and_1_out, and_2_out, and_3_out, and_4_out);
endmodule

module DeMux (
  input  sel_0,
  input  sel_1,
  input  e,
  output a,
  output b,
  output c,
  output d
);

  wire not_1_out, not_2_out, not_3_out, not_4_out;

  not not_1 (not_1_out, sel_1);
  not not_2 (not_2_out, sel_0);
  not not_3 (not_3_out, sel_1);
  not not_4 (not_4_out, sel_0);
  and and_1 (d, sel_1, sel_0, e);
  and and_2 (a, not_1_out, not_2_out, e);
  and and_3 (b, not_3_out, sel_0, e);
  and and_4 (c, sel_1, not_4_out, e);
endmodule

module MuDemux (
  input  sel_1,
  input  sel_0,
  input  A,
  input  B,
  input  C,
  input  D,
  output A_2,
  output B_2,
  output C_2,
  output D_2
);

  wire multiplexador_1_s;

  Multiplexador multiplexador_1 (.A(A), .B(B), .C(C), .D(D), .SEL_1(sel_1), .SEL_0(sel_0), .S(multiplexador_1_s));
  DeMux demux_1 (.sel_0(sel_0), .sel_1(sel_1), .e(multiplexador_1_s), .a(A_2), .b(B_2), .c(C_2), .d(D_2));

  // Other names for the same wires on the sheet: _0 = sel_0; _1 = sel_1
endmodule

module codificador_prioridade1 (
  input  x3,
  input  x2,
  input  x1,
  input  x0,
  output y1,
  output y0,
  output a
);

  wire and_1_out, and_2_out, not_1_out, not_2_out, not_3_out;

  and and_1 (and_1_out, x2, not_1_out);
  not not_1 (not_1_out, x3);
  and and_2 (and_2_out, x1, not_2_out, not_3_out);
  not not_2 (not_2_out, x2);
  not not_3 (not_3_out, x3);
  or or_1 (a, x0, x1, x2, x3);
  or or_2 (y1, and_1_out, x3);
  or or_3 (y0, and_2_out, x3);
endmodule

module cod_prio2 (
  input  x0,
  input  x1,
  input  x2,
  input  x3,
  input  x4,
  input  x5,
  output a,
  output y0,
  output y1,
  output y2
);

  wire and_1_out, and_2_out, and_3_out, and_4_out, not_1_out, not_2_out, not_3_out, not_4_out, not_5_out,
       not_6_out, not_7_out;

  or or_1 (a, x1, x2, x3, x4, x5);
  not not_1 (not_1_out, x3);
  not not_2 (not_2_out, x4);
  not not_3 (not_3_out, x5);
  not not_4 (not_4_out, x5);
  not not_5 (not_5_out, x4);
  not not_6 (not_6_out, x5);
  not not_7 (not_7_out, x5);
  and and_1 (and_1_out, x2, not_1_out, not_2_out, not_3_out);
  and and_2 (and_2_out, x4, not_4_out);
  and and_3 (and_3_out, x3, not_5_out, not_6_out);
  and and_4 (and_4_out, x4, not_7_out);
  or or_2 (y0, and_1_out, and_2_out);
  or or_3 (y1, and_3_out, and_4_out);

  assign y2 = x5;
endmodule

module decodificador1 (
  input  a,
  input  b,
  output s3,
  output s2,
  output s1,
  output s0
);

  wire not_1_out, not_2_out, not_3_out, not_4_out;

  and and_1 (s3, a, b);
  not not_1 (not_1_out, b);
  not not_2 (not_2_out, a);
  not not_3 (not_3_out, a);
  not not_4 (not_4_out, b);
  and and_2 (s2, a, not_1_out);
  and and_3 (s1, not_2_out, b);
  and and_4 (s0, not_3_out, not_4_out);
endmodule

module display7segmentos (
  input  a,
  input  b,
  input  c,
  input  d,
  output sa,
  output sb,
  output sc,
  output sd,
  output se,
  output sf,
  output sg,
  output dp
);

  wire and_1_out, and_2_out, and_3_out, and_4_out, and_5_out, and_6_out, and_7_out, and_8_out, and_9_out,
       and_10_out, and_11_out, and_12_out, and_13_out, and_14_out, and_15_out, and_16_out, and_17_out,
       and_18_out, and_19_out, and_20_out, and_21_out, and_22_out, and_23_out, and_24_out, and_25_out,
       and_26_out, and_27_out, and_28_out, and_29_out, and_30_out, and_31_out, and_32_out, and_33_out,
       and_34_out, and_35_out, not_1_out, not_2_out, not_3_out, not_4_out, not_5_out, not_6_out, not_7_out,
       not_8_out, not_9_out, not_10_out, not_11_out, not_12_out, not_13_out, not_14_out, not_15_out,
       not_16_out, not_17_out, not_18_out, not_19_out, not_20_out, not_21_out, not_22_out, not_23_out,
       not_24_out, not_25_out, not_26_out, not_27_out, not_28_out, not_29_out, not_30_out, not_31_out,
       not_32_out, not_33_out, not_34_out, not_35_out, not_36_out, not_37_out, not_38_out, not_39_out,
       not_40_out, not_41_out, not_42_out, not_43_out, not_44_out;

  not not_1 (not_1_out, b);
  and and_1 (and_1_out, not_1_out, not_2_out);
  not not_2 (not_2_out, d);
  not not_3 (not_3_out, a);
  and and_2 (and_2_out, not_3_out, c);
  not not_4 (not_4_out, a);
  and and_3 (and_3_out, not_4_out, b, d);
  and and_4 (and_4_out, b, c);
  not not_5 (not_5_out, b);
  and and_5 (and_5_out, a, not_5_out, not_6_out);
  not not_6 (not_6_out, c);
  and and_6 (and_6_out, a, not_7_out);
  not not_7 (not_7_out, d);
  not not_8 (not_8_out, a);
  and and_7 (and_7_out, not_8_out, not_9_out);
  not not_9 (not_9_out, b);
  not not_10 (not_10_out, a);
  not not_11 (not_11_out, c);
  and and_8 (and_8_out, not_10_out, not_11_out, not_12_out);
  not not_12 (not_12_out, d);
  not not_13 (not_13_out, b);
  and and_9 (and_9_out, not_13_out, not_14_out);
  not not_14 (not_14_out, d);
  not not_15 (not_15_out, a);
  and and_10 (and_10_out, not_15_out, c, d);
  and and_11 (and_11_out, a, not_16_out, d);
  not not_16 (not_16_out, c);
  not not_17 (not_17_out, a);
  and and_12 (and_12_out, not_17_out, not_18_out);
  not not_18 (not_18_out, c);
  not not_19 (not_19_out, a);
  and and_13 (and_13_out, not_19_out, d);
  not not_20 (not_20_out, c);
  and and_14 (and_14_out, not_20_out, d);
  not not_21 (not_21_out, a);
  and and_15 (and_15_out, not_21_out, b);
  and and_16 (and_16_out, a, not_22_out);
  not not_22 (not_22_out, b);
  not not_23 (not_23_out, a);
  not not_24 (not_24_out, b);
  and and_17 (and_17_out, not_23_out, not_24_out, not_25_out);
  not not_25 (not_25_out, d);
  not not_26 (not_26_out, b);
  and and_18 (and_18_out, not_26_out, c, d);
  not not_27 (not_27_out, c);
  and and_19 (and_19_out, b, not_27_out, d);
  and and_20 (and_20_out, b, c, not_28_out);
  not not_28 (not_28_out, d);
  not not_29 (not_29_out, c);
  and and_21 (and_21_out, a, not_29_out, not_30_out);
  not not_30 (not_30_out, d);
  not not_31 (not_31_out, b);
  and and_22 (and_22_out, not_31_out, not_32_out);
  not not_32 (not_32_out, d);
  and and_23 (and_23_out, c, not_33_out);
  not not_33 (not_33_out, d);
  and and_24 (and_24_out, a, c);
  and and_25 (and_25_out, a, b);
  not not_34 (not_34_out, c);
  and and_26 (and_26_out, not_34_out, not_35_out);
  not not_35 (not_35_out, d);
  not not_36 (not_36_out, a);
  and and_27 (and_27_out, not_36_out, b, not_37_out);
  not not_37 (not_37_out, c);
  and and_28 (and_28_out, b, not_38_out);
  not not_38 (not_38_out, d);
  and and_29 (and_29_out, a, not_39_out);
  not not_39 (not_39_out, b);
  and and_30 (and_30_out, a, c);
  not not_40 (not_40_out, b);
  and and_31 (and_31_out, not_40_out, c);
  and and_32 (and_32_out, c, not_41_out);
  not not_41 (not_41_out, d);
  not not_42 (not_42_out, a);
  and and_33 (and_33_out, not_42_out, b, not_43_out);
  not not_43 (not_43_out, c);
  and and_34 (and_34_out, a, not_44_out);
  not not_44 (not_44_out, b);
  and and_35 (and_35_out, a, d);
  or or_1 (sb, and_7_out, and_8_out, and_9_out, and_10_out, and_11_out);
  or or_2 (sc, and_12_out, and_13_out, and_14_out, and_15_out, and_16_out);
  or or_3 (sd, and_17_out, and_18_out, and_19_out, and_20_out, and_21_out);
  or or_4 (se, and_22_out, and_23_out, and_24_out, and_25_out);
  or or_5 (sf, and_26_out, and_27_out, and_28_out, and_29_out, and_30_out);
  or or_6 (sg, and_31_out, and_32_out, and_33_out, and_34_out, and_35_out);
  or or_7 (sa, and_1_out, and_2_out, and_3_out, and_4_out, and_5_out, and_6_out);

  assign dp = 1'b0;
endmodule

module _7seg (
  input  A,
  input  B,
  input  C,
  input  D
);

  wire display7segmentos_1_dp, display7segmentos_1_sa, display7segmentos_1_sb, display7segmentos_1_sc,
       display7segmentos_1_sd, display7segmentos_1_se, display7segmentos_1_sf, display7segmentos_1_sg;

  display7segmentos display7segmentos_1 (
    .a(A), .b(B), .c(C), .d(D), .sa(display7segmentos_1_sa), .sb(display7segmentos_1_sb),
    .sc(display7segmentos_1_sc), .sd(display7segmentos_1_sd), .se(display7segmentos_1_se),
    .sf(display7segmentos_1_sf), .sg(display7segmentos_1_sg), .dp(display7segmentos_1_dp));
  _7_Segment_Display u_7_segment_display_1 (
    .g(display7segmentos_1_sg), .f(display7segmentos_1_sf), .a(display7segmentos_1_sa),
    .b(display7segmentos_1_sb), .e(display7segmentos_1_se), .d(display7segmentos_1_sd),
    .c(display7segmentos_1_sc), .dp(display7segmentos_1_dp));
endmodule

module _31_08 (
  input  A,
  input  in_2,
  input  in_3,
  input  B
);

  wire and_1_out, nand_1_out, or_1_out, xor_1_out;
  wire [0:0] multiplexador_1_s;

  or or_1 (or_1_out, A, B);
  nand nand_1 (nand_1_out, A, B);
  and and_1 (and_1_out, A, B);
  xor xor_1 (xor_1_out, A, B);
  Multiplexador multiplexador_1 (
    .A(or_1_out), .B(nand_1_out), .C(and_1_out), .D(xor_1_out), .SEL_1(in_2), .SEL_0(in_3),
    .S(multiplexador_1_s[0]));
  Hex_Digit_Display hex_digit_display_1 (.value({3'b000, multiplexador_1_s[0]}));  // open: dp
endmodule

module contador_assincrono (
  input  in_1,
  output s1,
  output s2,
  output s0,
  output s3
);

  wire not_1_out, not_2_out, not_3_out, not_4_out;

  not not_1 (not_1_out, in_1);
  J_K_Flip_Flop j_k_ff_1 (
    .J(1'b1), .clk(not_1_out), .K(1'b1), .Q(s0), .preset(1'b0), .en(1'b1), .reset(1'b0));  // open: Qn
  not not_2 (not_2_out, s0);
  J_K_Flip_Flop j_k_ff_2 (
    .J(1'b1), .clk(not_2_out), .K(1'b1), .Q(s1), .preset(1'b0), .en(1'b1), .reset(1'b0));  // open: Qn
  not not_3 (not_3_out, s1);
  J_K_Flip_Flop j_k_ff_3 (
    .J(1'b1), .clk(not_3_out), .K(1'b1), .Q(s2), .preset(1'b0), .en(1'b1), .reset(1'b0));  // open: Qn
  not not_4 (not_4_out, s2);
  J_K_Flip_Flop j_k_ff_4 (
    .J(1'b1), .clk(not_4_out), .K(1'b1), .Q(s3), .preset(1'b0), .en(1'b1), .reset(1'b0));  // open: Qn
endmodule

module contador_7seg (
);

  wire contador_assincrono_1_s0, contador_assincrono_1_s1, contador_assincrono_1_s2,
       contador_assincrono_1_s3, display7segmentos_1_dp, display7segmentos_1_sa, display7segmentos_1_sb,
       display7segmentos_1_sc, display7segmentos_1_sd, display7segmentos_1_se, display7segmentos_1_sf,
       display7segmentos_1_sg;

  contador_assincrono contador_assincrono_1 (
    .s0(contador_assincrono_1_s0), .s1(contador_assincrono_1_s1), .s2(contador_assincrono_1_s2),
    .s3(contador_assincrono_1_s3));  // open: in_1
  display7segmentos display7segmentos_1 (
    .a(contador_assincrono_1_s3), .b(contador_assincrono_1_s2), .c(contador_assincrono_1_s1),
    .d(contador_assincrono_1_s0), .sa(display7segmentos_1_sa), .sb(display7segmentos_1_sb),
    .sc(display7segmentos_1_sc), .sd(display7segmentos_1_sd), .se(display7segmentos_1_se),
    .sf(display7segmentos_1_sf), .sg(display7segmentos_1_sg), .dp(display7segmentos_1_dp));
  _7_Segment_Display u_7_segment_display_1 (
    .g(display7segmentos_1_sg), .f(display7segmentos_1_sf), .a(display7segmentos_1_sa),
    .b(display7segmentos_1_sb), .e(display7segmentos_1_se), .d(display7segmentos_1_sd),
    .c(display7segmentos_1_sc), .dp(display7segmentos_1_dp));
endmodule

module contador_assinc_decada (
  output s1,
  output s2,
  output s5,
  output s0,
  output s6,
  output s3,
  output s4,
  output s7
);

  wire and_1_out, and_2_out, clock_1_out, j_k_ff_1_qn, j_k_ff_3_qn, j_k_ff_5_qn, j_k_ff_7_qn, not_1_out,
       not_2_out, not_3_out, not_4_out, not_5_out, not_6_out, not_7_out, not_8_out, not_9_out, not_10_out,
       not_11_out, not_12_out;

  not not_1 (not_1_out, clock_1_out);
  Clock clock_1 (.out(clock_1_out));
  J_K_Flip_Flop j_k_ff_1 (
    .J(1'b1), .clk(not_1_out), .K(1'b1), .Q(s0), .Qn(j_k_ff_1_qn), .preset(1'b0), .en(1'b1), .reset(not_5_out));
  not not_2 (not_2_out, s0);
  J_K_Flip_Flop j_k_ff_2 (
    .J(1'b1), .clk(not_2_out), .K(1'b1), .Q(s1), .preset(1'b0), .en(1'b1), .reset(not_5_out));  // open: Qn
  not not_3 (not_3_out, s1);
  J_K_Flip_Flop j_k_ff_3 (
    .J(1'b1), .clk(not_3_out), .K(1'b1), .Q(s2), .Qn(j_k_ff_3_qn), .preset(1'b0), .en(1'b1), .reset(not_5_out));
  not not_4 (not_4_out, s2);
  J_K_Flip_Flop j_k_ff_4 (
    .J(1'b1), .clk(not_4_out), .K(1'b1), .Q(s3), .preset(1'b0), .en(1'b1), .reset(not_5_out));  // open: Qn
  and and_1 (and_1_out, s3, s1, j_k_ff_3_qn, j_k_ff_1_qn);
  not not_5 (not_5_out, not_6_out);
  not not_6 (not_6_out, and_1_out);
  not not_7 (not_7_out, not_5_out);
  J_K_Flip_Flop j_k_ff_5 (
    .J(1'b1), .clk(not_7_out), .K(1'b1), .Q(s4), .Qn(j_k_ff_5_qn), .preset(1'b0), .en(1'b1),
    .reset(not_11_out));
  not not_8 (not_8_out, s4);
  J_K_Flip_Flop j_k_ff_6 (
    .J(1'b1), .clk(not_8_out), .K(1'b1), .Q(s5), .preset(1'b0), .en(1'b1), .reset(not_11_out));  // open: Qn
  not not_9 (not_9_out, s5);
  not not_10 (not_10_out, s6);
  J_K_Flip_Flop j_k_ff_7 (
    .J(1'b1), .clk(not_9_out), .K(1'b1), .Q(s6), .Qn(j_k_ff_7_qn), .preset(1'b0), .en(1'b1),
    .reset(not_11_out));
  J_K_Flip_Flop j_k_ff_8 (
    .J(1'b1), .clk(not_10_out), .K(1'b1), .Q(s7), .preset(1'b0), .en(1'b1), .reset(not_11_out));  // open: Qn
  not not_11 (not_11_out, not_12_out);
  not not_12 (not_12_out, and_2_out);
  and and_2 (and_2_out, s7, s5, j_k_ff_7_qn, j_k_ff_5_qn);
endmodule

module contador99 (
);

  wire assincrono_decada_errado_1_s0, assincrono_decada_errado_1_s1, assincrono_decada_errado_1_s2,
       assincrono_decada_errado_1_s3, contador_assinc_decada_1_s0, contador_assinc_decada_1_s1,
       contador_assinc_decada_1_s2, contador_assinc_decada_1_s3, contador_assinc_decada_1_s4,
       contador_assinc_decada_1_s5, contador_assinc_decada_1_s6, contador_assinc_decada_1_s7,
       display7segmentos_1_dp, display7segmentos_1_sa, display7segmentos_1_sb, display7segmentos_1_sc,
       display7segmentos_1_sd, display7segmentos_1_se, display7segmentos_1_sf, display7segmentos_1_sg,
       display7segmentos_2_dp, display7segmentos_2_sa, display7segmentos_2_sb, display7segmentos_2_sc,
       display7segmentos_2_sd, display7segmentos_2_se, display7segmentos_2_sf, display7segmentos_2_sg,
       display7segmentos_3_dp, display7segmentos_3_sa, display7segmentos_3_sb, display7segmentos_3_sc,
       display7segmentos_3_sd, display7segmentos_3_se, display7segmentos_3_sf, display7segmentos_3_sg;

  assincrono_decada_errado assincrono_decada_errado_1 (
    .s0(assincrono_decada_errado_1_s0), .s1(assincrono_decada_errado_1_s1),
    .s2(assincrono_decada_errado_1_s2), .s3(assincrono_decada_errado_1_s3));
  display7segmentos display7segmentos_1 (
    .a(contador_assinc_decada_1_s7), .b(contador_assinc_decada_1_s6), .c(contador_assinc_decada_1_s5),
    .d(contador_assinc_decada_1_s4), .sa(display7segmentos_1_sa), .sb(display7segmentos_1_sb),
    .sc(display7segmentos_1_sc), .sd(display7segmentos_1_sd), .se(display7segmentos_1_se),
    .sf(display7segmentos_1_sf), .sg(display7segmentos_1_sg), .dp(display7segmentos_1_dp));
  _7_Segment_Display u_7_segment_display_1 (
    .g(display7segmentos_1_sg), .f(display7segmentos_1_sf), .a(display7segmentos_1_sa),
    .b(display7segmentos_1_sb), .e(display7segmentos_1_se), .d(display7segmentos_1_sd),
    .c(display7segmentos_1_sc), .dp(display7segmentos_1_dp));
  contador_assinc_decada contador_assinc_decada_1 (
    .s0(contador_assinc_decada_1_s0), .s1(contador_assinc_decada_1_s1), .s2(contador_assinc_decada_1_s2),
    .s3(contador_assinc_decada_1_s3), .s4(contador_assinc_decada_1_s4), .s5(contador_assinc_decada_1_s5),
    .s6(contador_assinc_decada_1_s6), .s7(contador_assinc_decada_1_s7));
  display7segmentos display7segmentos_2 (
    .a(assincrono_decada_errado_1_s3), .b(assincrono_decada_errado_1_s2), .c(assincrono_decada_errado_1_s1),
    .d(assincrono_decada_errado_1_s0), .sa(display7segmentos_2_sa), .sb(display7segmentos_2_sb),
    .sc(display7segmentos_2_sc), .sd(display7segmentos_2_sd), .se(display7segmentos_2_se),
    .sf(display7segmentos_2_sf), .sg(display7segmentos_2_sg), .dp(display7segmentos_2_dp));
  display7segmentos display7segmentos_3 (
    .a(contador_assinc_decada_1_s3), .b(contador_assinc_decada_1_s2), .c(contador_assinc_decada_1_s1),
    .d(contador_assinc_decada_1_s0), .sa(display7segmentos_3_sa), .sb(display7segmentos_3_sb),
    .sc(display7segmentos_3_sc), .sd(display7segmentos_3_sd), .se(display7segmentos_3_se),
    .sf(display7segmentos_3_sf), .sg(display7segmentos_3_sg), .dp(display7segmentos_3_dp));
  _7_Segment_Display u_7_segment_display_2 (
    .g(display7segmentos_2_sg), .f(display7segmentos_2_sf), .a(display7segmentos_2_sa),
    .b(display7segmentos_2_sb), .e(display7segmentos_2_se), .d(display7segmentos_2_sd),
    .c(display7segmentos_2_sc), .dp(display7segmentos_2_dp));
  _7_Segment_Display u_7_segment_display_3 (
    .g(display7segmentos_3_sg), .f(display7segmentos_3_sf), .a(display7segmentos_3_sa),
    .b(display7segmentos_3_sb), .e(display7segmentos_3_se), .d(display7segmentos_3_sd),
    .c(display7segmentos_3_sc), .dp(display7segmentos_3_dp));
endmodule

module assincrono_decada_errado (
  output s1,
  output s2,
  output s0,
  output s3
);

  wire and_1_out, clock_1_out, j_k_ff_1_qn, j_k_ff_3_qn, not_1_out, not_2_out, not_3_out, not_4_out;

  not not_1 (not_1_out, clock_1_out);
  Clock clock_1 (.out(clock_1_out));
  J_K_Flip_Flop j_k_ff_1 (
    .J(1'b1), .clk(not_1_out), .K(1'b1), .Q(s0), .Qn(j_k_ff_1_qn), .preset(1'b0), .en(1'b1), .reset(and_1_out));
  not not_2 (not_2_out, s0);
  J_K_Flip_Flop j_k_ff_2 (
    .J(1'b1), .clk(not_2_out), .K(1'b1), .Q(s1), .preset(1'b0), .en(1'b1), .reset(and_1_out));  // open: Qn
  J_K_Flip_Flop j_k_ff_3 (
    .J(1'b1), .clk(not_3_out), .K(1'b1), .Q(s2), .Qn(j_k_ff_3_qn), .preset(1'b0), .en(1'b1), .reset(and_1_out));
  not not_3 (not_3_out, s1);
  not not_4 (not_4_out, s2);
  J_K_Flip_Flop j_k_ff_4 (
    .J(1'b1), .clk(not_4_out), .K(1'b1), .Q(s3), .preset(1'b0), .en(1'b1), .reset(and_1_out));  // open: Qn
  and and_1 (and_1_out, s3, s1, j_k_ff_3_qn, j_k_ff_1_qn);
endmodule

module _0_13 (
  output s1,
  output s2,
  output s0,
  output s3
);

  wire and_1_out, clock_1_out, j_k_ff_1_qn, not_1_out, not_2_out, not_3_out, not_4_out, not_5_out, not_6_out;

  not not_1 (not_1_out, clock_1_out);
  Clock clock_1 (.out(clock_1_out));
  J_K_Flip_Flop j_k_ff_1 (
    .J(1'b1), .clk(not_1_out), .K(1'b1), .Q(s0), .Qn(j_k_ff_1_qn), .preset(1'b0), .en(1'b1), .reset(not_5_out));
  not not_2 (not_2_out, s0);
  J_K_Flip_Flop j_k_ff_2 (
    .J(1'b1), .clk(not_2_out), .K(1'b1), .Q(s1), .preset(1'b0), .en(1'b1), .reset(not_5_out));  // open: Qn
  not not_3 (not_3_out, s1);
  J_K_Flip_Flop j_k_ff_3 (
    .J(1'b1), .clk(not_3_out), .K(1'b1), .Q(s2), .preset(1'b0), .en(1'b1), .reset(not_5_out));  // open: Qn
  not not_4 (not_4_out, s2);
  J_K_Flip_Flop j_k_ff_4 (
    .J(1'b1), .clk(not_4_out), .K(1'b1), .Q(s3), .preset(1'b0), .en(1'b1), .reset(not_5_out));  // open: Qn
  and and_1 (and_1_out, s3, s1, s2, j_k_ff_1_qn);
  not not_5 (not_5_out, not_6_out);
  not not_6 (not_6_out, and_1_out);
endmodule

module contador_0_13 (
);

  wire display7segmentos_1_dp, display7segmentos_1_sa, display7segmentos_1_sb, display7segmentos_1_sc,
       display7segmentos_1_sd, display7segmentos_1_se, display7segmentos_1_sf, display7segmentos_1_sg,
       n0_13_1_s0, n0_13_1_s1, n0_13_1_s2, n0_13_1_s3;

  _0_13 u_0_13_1 (.s0(n0_13_1_s0), .s1(n0_13_1_s1), .s2(n0_13_1_s2), .s3(n0_13_1_s3));
  display7segmentos display7segmentos_1 (
    .a(n0_13_1_s3), .b(n0_13_1_s2), .c(n0_13_1_s1), .d(n0_13_1_s0), .sa(display7segmentos_1_sa),
    .sb(display7segmentos_1_sb), .sc(display7segmentos_1_sc), .sd(display7segmentos_1_sd),
    .se(display7segmentos_1_se), .sf(display7segmentos_1_sf), .sg(display7segmentos_1_sg),
    .dp(display7segmentos_1_dp));
  _7_Segment_Display u_7_segment_display_1 (
    .g(display7segmentos_1_sg), .f(display7segmentos_1_sf), .a(display7segmentos_1_sa),
    .b(display7segmentos_1_sb), .e(display7segmentos_1_se), .d(display7segmentos_1_sd),
    .c(display7segmentos_1_sc), .dp(display7segmentos_1_dp));
endmodule

module contador_dcr_cre (
  input  controle,
  output Q0,
  output Q1,
  output Q2,
  output Q3
);

  wire clock_1_out, not_1_out, xnor_1_out, xnor_2_out, xnor_3_out;

  Clock clock_1 (.out(clock_1_out));
  not not_1 (not_1_out, clock_1_out);
  J_K_Flip_Flop j_k_ff_1 (.J(1'b1), .clk(not_1_out), .K(1'b1), .Q(Q0));  // open: Qn, preset, en, reset
  xnor xnor_1 (xnor_1_out, Q0, controle);
  J_K_Flip_Flop j_k_ff_2 (.J(1'b1), .clk(xnor_1_out), .K(1'b1), .Q(Q1));  // open: Qn, preset, en, reset
  xnor xnor_2 (xnor_2_out, Q1, controle);
  J_K_Flip_Flop j_k_ff_3 (.J(1'b1), .clk(xnor_2_out), .K(1'b1), .Q(Q2));  // open: Qn, preset, en, reset
  xnor xnor_3 (xnor_3_out, Q2, controle);
  J_K_Flip_Flop j_k_ff_4 (.J(1'b1), .clk(xnor_3_out), .K(1'b1), .Q(Q3));  // open: Qn, preset, en, reset
endmodule

module _0_15___15_0 (
  input  C_D
);

  wire contador_dcr_cre_1_q0, contador_dcr_cre_1_q1, contador_dcr_cre_1_q2, contador_dcr_cre_1_q3,
       display7segmentos_1_dp, display7segmentos_1_sa, display7segmentos_1_sb, display7segmentos_1_sc,
       display7segmentos_1_sd, display7segmentos_1_se, display7segmentos_1_sf, display7segmentos_1_sg;

  contador_dcr_cre contador_dcr_cre_1 (
    .controle(C_D), .Q0(contador_dcr_cre_1_q0), .Q1(contador_dcr_cre_1_q1), .Q2(contador_dcr_cre_1_q2),
    .Q3(contador_dcr_cre_1_q3));
  display7segmentos display7segmentos_1 (
    .a(contador_dcr_cre_1_q3), .b(contador_dcr_cre_1_q2), .c(contador_dcr_cre_1_q1),
    .d(contador_dcr_cre_1_q0), .sa(display7segmentos_1_sa), .sb(display7segmentos_1_sb),
    .sc(display7segmentos_1_sc), .sd(display7segmentos_1_sd), .se(display7segmentos_1_se),
    .sf(display7segmentos_1_sf), .sg(display7segmentos_1_sg), .dp(display7segmentos_1_dp));
  _7_Segment_Display u_7_segment_display_1 (
    .g(display7segmentos_1_sg), .f(display7segmentos_1_sf), .a(display7segmentos_1_sa),
    .b(display7segmentos_1_sb), .e(display7segmentos_1_se), .d(display7segmentos_1_sd),
    .c(display7segmentos_1_sc), .dp(display7segmentos_1_dp));
endmodule

// PRESET
module flipflop_inicia (
  input  A,
  input  INICIO,
  output preset,
  output clear
);

  wire not_1_out;

  and and_1 (preset, A, INICIO);
  not not_1 (not_1_out, preset);
  and and_2 (clear, not_1_out, INICIO);
endmodule

module _0_17_inicio_6 (
  input  INICIO,
  input  A0,
  input  A1,
  input  A2,
  input  A3,
  input  A4,
  output out_7,
  output out_8,
  output out_9,
  output out_10,
  output out_11
);

  wire and_1_out, clock_1_out, flipflop_inicia_1_clear, flipflop_inicia_1_preset, flipflop_inicia_2_clear,
       flipflop_inicia_2_preset, flipflop_inicia_3_clear, flipflop_inicia_3_preset, flipflop_inicia_4_clear,
       flipflop_inicia_4_preset, flipflop_inicia_5_clear, flipflop_inicia_5_preset, j_k_ff_1_qn, j_k_ff_3_qn,
       j_k_ff_4_qn, not_1_out, not_2_out, not_3_out, not_4_out, not_5_out, not_6_out, not_7_out, or_1_out,
       or_2_out, or_3_out, or_4_out, or_5_out;

  not not_1 (not_1_out, clock_1_out);
  Clock clock_1 (.out(clock_1_out));
  flipflop_inicia flipflop_inicia_1 (
    .A(A0), .INICIO(INICIO), .preset(flipflop_inicia_1_preset), .clear(flipflop_inicia_1_clear));
  J_K_Flip_Flop j_k_ff_1 (
    .J(1'b1), .clk(not_1_out), .K(1'b1), .Q(out_11), .Qn(j_k_ff_1_qn), .preset(flipflop_inicia_1_preset),
    .en(1'b1), .reset(or_1_out));
  or or_1 (or_1_out, flipflop_inicia_1_clear, not_6_out);
  not not_2 (not_2_out, out_11);
  or or_2 (or_2_out, not_6_out, flipflop_inicia_2_clear);
  flipflop_inicia flipflop_inicia_2 (
    .A(A1), .INICIO(INICIO), .preset(flipflop_inicia_2_preset), .clear(flipflop_inicia_2_clear));
  J_K_Flip_Flop j_k_ff_2 (
    .J(1'b1), .clk(not_2_out), .K(1'b1), .Q(out_7), .preset(flipflop_inicia_2_preset), .en(1'b1),
    .reset(or_2_out));  // open: Qn
  not not_3 (not_3_out, out_7);
  J_K_Flip_Flop j_k_ff_3 (
    .J(1'b1), .clk(not_3_out), .K(1'b1), .Q(out_8), .Qn(j_k_ff_3_qn), .preset(flipflop_inicia_3_preset),
    .en(1'b1), .reset(or_3_out));
  flipflop_inicia flipflop_inicia_3 (
    .A(A2), .INICIO(INICIO), .preset(flipflop_inicia_3_preset), .clear(flipflop_inicia_3_clear));
  not not_4 (not_4_out, out_8);
  or or_3 (or_3_out, not_6_out, flipflop_inicia_3_clear);
  J_K_Flip_Flop j_k_ff_4 (
    .J(1'b1), .clk(not_4_out), .K(1'b1), .Q(out_9), .Qn(j_k_ff_4_qn), .preset(flipflop_inicia_4_preset),
    .en(1'b1), .reset(or_4_out));
  flipflop_inicia flipflop_inicia_4 (
    .A(A3), .INICIO(INICIO), .preset(flipflop_inicia_4_preset), .clear(flipflop_inicia_4_clear));
  not not_5 (not_5_out, out_9);
  or or_4 (or_4_out, not_6_out, flipflop_inicia_4_clear);
  J_K_Flip_Flop j_k_ff_5 (
    .J(1'b1), .clk(not_5_out), .K(1'b1), .Q(out_10), .preset(flipflop_inicia_5_preset), .en(1'b1),
    .reset(or_5_out));  // open: Qn
  or or_5 (or_5_out, not_6_out, flipflop_inicia_5_clear);
  flipflop_inicia flipflop_inicia_5 (
    .A(A4), .INICIO(INICIO), .preset(flipflop_inicia_5_preset), .clear(flipflop_inicia_5_clear));
  not not_6 (not_6_out, not_7_out);
  not not_7 (not_7_out, and_1_out);
  and and_1 (and_1_out, out_10, j_k_ff_4_qn, j_k_ff_3_qn, out_7, j_k_ff_1_qn);
endmodule

module ct_decada_sinc (
  output Q0,
  output Q1,
  output Q2,
  output Q3
);

  wire and_1_out, and_2_out, and_3_out, clock_1_out, j_k_ff_1_qn, j_k_ff_3_qn, not_1_out, not_2_out,
       not_3_out;

  Clock clock_1 (.out(clock_1_out));
  not not_1 (not_1_out, clock_1_out);
  J_K_Flip_Flop j_k_ff_1 (
    .J(1'b1), .clk(not_1_out), .K(1'b1), .Q(Q0), .Qn(j_k_ff_1_qn), .preset(1'b0), .en(1'b1), .reset(not_2_out));
  J_K_Flip_Flop j_k_ff_2 (
    .J(Q0), .clk(not_1_out), .K(Q0), .Q(Q1), .preset(1'b0), .en(1'b1), .reset(not_2_out));  // open: Qn
  and and_1 (and_1_out, Q0, Q1);
  J_K_Flip_Flop j_k_ff_3 (
    .J(and_1_out), .clk(not_1_out), .K(and_1_out), .Q(Q2), .Qn(j_k_ff_3_qn), .preset(1'b0), .en(1'b1),
    .reset(not_2_out));
  and and_2 (and_2_out, and_1_out, Q2);
  J_K_Flip_Flop j_k_ff_4 (
    .J(and_2_out), .clk(not_1_out), .K(and_2_out), .Q(Q3), .preset(1'b0), .en(1'b1), .reset(not_2_out));  // open: Qn
  and and_3 (and_3_out, Q3, j_k_ff_3_qn, Q1, j_k_ff_1_qn);
  not not_2 (not_2_out, not_3_out);
  not not_3 (not_3_out, and_3_out);
endmodule

module _0_18_SINC (
  output Q0,
  output Q1,
  output Q2,
  output Q3,
  output Q4
);

  wire and_1_out, and_2_out, and_3_out, and_4_out, clock_1_out, j_k_ff_3_qn, j_k_ff_4_qn, not_1_out,
       not_2_out, not_3_out;

  Clock clock_1 (.out(clock_1_out));
  not not_1 (not_1_out, clock_1_out);
  J_K_Flip_Flop j_k_ff_1 (
    .J(1'b1), .clk(not_1_out), .K(1'b1), .Q(Q0), .preset(1'b0), .en(1'b1), .reset(not_2_out));  // open: Qn
  J_K_Flip_Flop j_k_ff_2 (
    .J(Q0), .clk(not_1_out), .K(Q0), .Q(Q1), .preset(1'b0), .en(1'b1), .reset(not_2_out));  // open: Qn
  and and_1 (and_1_out, Q0, Q1);
  J_K_Flip_Flop j_k_ff_3 (
    .J(and_1_out), .clk(not_1_out), .K(and_1_out), .Q(Q2), .Qn(j_k_ff_3_qn), .preset(1'b0), .en(1'b1),
    .reset(not_2_out));
  and and_2 (and_2_out, and_1_out, Q2);
  J_K_Flip_Flop j_k_ff_4 (
    .J(and_2_out), .clk(not_1_out), .K(and_2_out), .Q(Q3), .Qn(j_k_ff_4_qn), .preset(1'b0), .en(1'b1),
    .reset(not_2_out));
  and and_3 (and_3_out, and_2_out, Q3);
  J_K_Flip_Flop j_k_ff_5 (
    .J(and_3_out), .clk(not_1_out), .K(and_3_out), .Q(Q4), .preset(1'b0), .en(1'b1), .reset(not_2_out));  // open: Qn
  and and_4 (and_4_out, Q4, j_k_ff_4_qn, j_k_ff_3_qn, Q1, Q0);
  not not_2 (not_2_out, not_3_out);
  not not_3 (not_3_out, and_4_out);
endmodule

module _0_13_SINC_HEX (
  output Q0,
  output Q1,
  output Q2,
  output Q3
);

  wire and_1_out, and_2_out, and_3_out, clock_1_out, j_k_ff_1_qn, not_1_out, not_2_out, not_3_out;

  Clock clock_1 (.out(clock_1_out));
  not not_1 (not_1_out, clock_1_out);
  J_K_Flip_Flop j_k_ff_1 (
    .J(1'b1), .clk(not_1_out), .K(1'b1), .Q(Q0), .Qn(j_k_ff_1_qn), .preset(1'b0), .en(1'b1), .reset(not_2_out));
  J_K_Flip_Flop j_k_ff_2 (
    .J(Q0), .clk(not_1_out), .K(Q0), .Q(Q1), .preset(1'b0), .en(1'b1), .reset(not_2_out));  // open: Qn
  and and_1 (and_1_out, Q0, Q1);
  J_K_Flip_Flop j_k_ff_3 (
    .J(and_1_out), .clk(not_1_out), .K(and_1_out), .Q(Q2), .preset(1'b0), .en(1'b1), .reset(not_2_out));  // open: Qn
  and and_2 (and_2_out, and_1_out, Q2);
  J_K_Flip_Flop j_k_ff_4 (
    .J(and_2_out), .clk(not_1_out), .K(and_2_out), .Q(Q3), .preset(1'b0), .en(1'b1), .reset(not_2_out));  // open: Qn
  and and_3 (and_3_out, Q3, Q2, Q1, j_k_ff_1_qn);
  not not_2 (not_2_out, not_3_out);
  not not_3 (not_3_out, and_3_out);
endmodule

module _0_13_SINC_DEC (
  output Q4,
  output Q5,
  output Q6,
  output Q7,
  output Q0,
  output Q1,
  output Q2,
  output Q3
);

  wire and_1_out, and_2_out, and_3_out, and_4_out, and_5_out, and_6_out, and_7_out, and_8_out, clock_1_out,
       j_k_ff_1_qn, j_k_ff_2_qn, j_k_ff_4_qn, j_k_ff_5_qn, j_k_ff_6_qn, j_k_ff_7_qn, j_k_ff_8_qn, not_1_out,
       not_2_out, not_3_out, not_4_out, not_5_out, not_6_out, not_7_out, or_1_out;

  Clock clock_1 (.out(clock_1_out));
  not not_1 (not_1_out, clock_1_out);
  J_K_Flip_Flop j_k_ff_1 (
    .J(1'b1), .clk(or_1_out), .K(1'b1), .Q(Q4), .Qn(j_k_ff_1_qn), .preset(1'b0), .en(1'b1), .reset(not_3_out));
  J_K_Flip_Flop j_k_ff_2 (
    .J(1'b1), .clk(not_1_out), .K(1'b1), .Q(Q0), .Qn(j_k_ff_2_qn), .preset(1'b0), .en(1'b1), .reset(or_1_out));
  J_K_Flip_Flop j_k_ff_3 (
    .J(Q4), .clk(or_1_out), .K(Q4), .Q(Q5), .preset(1'b0), .en(1'b1), .reset(not_3_out));  // open: Qn
  and and_1 (and_1_out, Q0, Q1);
  J_K_Flip_Flop j_k_ff_4 (
    .J(Q0), .clk(not_1_out), .K(Q0), .Q(Q1), .Qn(j_k_ff_4_qn), .preset(1'b0), .en(1'b1), .reset(or_1_out));
  and and_2 (and_2_out, Q4, Q5);
  J_K_Flip_Flop j_k_ff_5 (
    .J(and_2_out), .clk(or_1_out), .K(and_2_out), .Q(Q6), .Qn(j_k_ff_5_qn), .preset(1'b0), .en(1'b1),
    .reset(not_3_out));
  J_K_Flip_Flop j_k_ff_6 (
    .J(and_1_out), .clk(not_1_out), .K(and_1_out), .Q(Q2), .Qn(j_k_ff_6_qn), .preset(1'b0), .en(1'b1),
    .reset(or_1_out));
  and and_3 (and_3_out, and_2_out, Q6);
  and and_4 (and_4_out, and_1_out, Q2);
  J_K_Flip_Flop j_k_ff_7 (
    .J(and_3_out), .clk(or_1_out), .K(and_3_out), .Q(Q7), .Qn(j_k_ff_7_qn), .preset(1'b0), .en(1'b1),
    .reset(not_3_out));
  J_K_Flip_Flop j_k_ff_8 (
    .J(and_4_out), .clk(not_1_out), .K(and_4_out), .Q(Q3), .Qn(j_k_ff_8_qn), .preset(1'b0), .en(1'b1),
    .reset(or_1_out));
  and and_5 (and_5_out, j_k_ff_7_qn, j_k_ff_5_qn, Q5, j_k_ff_1_qn);
  not not_2 (not_2_out, and_6_out);
  and and_6 (and_6_out, Q3, j_k_ff_6_qn, Q1, j_k_ff_2_qn);
  and and_7 (and_7_out, j_k_ff_8_qn, Q2, j_k_ff_2_qn, j_k_ff_4_qn);
  not not_3 (not_3_out, not_4_out);
  not not_4 (not_4_out, and_5_out);
  not not_5 (not_5_out, not_2_out);
  not not_6 (not_6_out, and_7_out);
  not not_7 (not_7_out, not_6_out);
  or or_1 (or_1_out, not_5_out, and_8_out);
  and and_8 (and_8_out, not_7_out, Q4);
endmodule

module DISPLAY_0_13 (
);

  wire display7segmentos_1_dp, display7segmentos_1_sa, display7segmentos_1_sb, display7segmentos_1_sc,
       display7segmentos_1_sd, display7segmentos_1_se, display7segmentos_1_sf, display7segmentos_1_sg,
       display7segmentos_2_dp, display7segmentos_2_sa, display7segmentos_2_sb, display7segmentos_2_sc,
       display7segmentos_2_sd, display7segmentos_2_se, display7segmentos_2_sf, display7segmentos_2_sg,
       display7segmentos_3_dp, display7segmentos_3_sa, display7segmentos_3_sb, display7segmentos_3_sc,
       display7segmentos_3_sd, display7segmentos_3_se, display7segmentos_3_sf, display7segmentos_3_sg,
       n0_13_sinc_dec_1_q0, n0_13_sinc_dec_1_q1, n0_13_sinc_dec_1_q2, n0_13_sinc_dec_1_q3,
       n0_13_sinc_dec_1_q4, n0_13_sinc_dec_1_q5, n0_13_sinc_dec_1_q6, n0_13_sinc_dec_1_q7,
       n0_13_sinc_hex_1_q0, n0_13_sinc_hex_1_q1, n0_13_sinc_hex_1_q2, n0_13_sinc_hex_1_q3;

  _0_13_SINC_HEX u_0_13_sinc_hex_1 (
    .Q0(n0_13_sinc_hex_1_q0), .Q1(n0_13_sinc_hex_1_q1), .Q2(n0_13_sinc_hex_1_q2), .Q3(n0_13_sinc_hex_1_q3));
  _0_13_SINC_DEC u_0_13_sinc_dec_1 (
    .Q0(n0_13_sinc_dec_1_q0), .Q4(n0_13_sinc_dec_1_q4), .Q1(n0_13_sinc_dec_1_q1), .Q5(n0_13_sinc_dec_1_q5),
    .Q2(n0_13_sinc_dec_1_q2), .Q6(n0_13_sinc_dec_1_q6), .Q3(n0_13_sinc_dec_1_q3), .Q7(n0_13_sinc_dec_1_q7));
  display7segmentos display7segmentos_1 (
    .a(n0_13_sinc_hex_1_q3), .b(n0_13_sinc_hex_1_q2), .c(n0_13_sinc_hex_1_q1), .d(n0_13_sinc_hex_1_q0),
    .sa(display7segmentos_1_sa), .sb(display7segmentos_1_sb), .sc(display7segmentos_1_sc),
    .sd(display7segmentos_1_sd), .se(display7segmentos_1_se), .sf(display7segmentos_1_sf),
    .sg(display7segmentos_1_sg), .dp(display7segmentos_1_dp));
  display7segmentos display7segmentos_2 (
    .a(n0_13_sinc_dec_1_q7), .b(n0_13_sinc_dec_1_q6), .c(n0_13_sinc_dec_1_q5), .d(n0_13_sinc_dec_1_q4),
    .sa(display7segmentos_2_sa), .sb(display7segmentos_2_sb), .sc(display7segmentos_2_sc),
    .sd(display7segmentos_2_sd), .se(display7segmentos_2_se), .sf(display7segmentos_2_sf),
    .sg(display7segmentos_2_sg), .dp(display7segmentos_2_dp));
  _7_Segment_Display u_7_segment_display_1 (
    .g(display7segmentos_1_sg), .f(display7segmentos_1_sf), .a(display7segmentos_1_sa),
    .b(display7segmentos_1_sb), .e(display7segmentos_1_se), .d(display7segmentos_1_sd),
    .c(display7segmentos_1_sc), .dp(display7segmentos_1_dp));
  _7_Segment_Display u_7_segment_display_2 (
    .g(display7segmentos_2_sg), .f(display7segmentos_2_sf), .a(display7segmentos_2_sa),
    .b(display7segmentos_2_sb), .e(display7segmentos_2_se), .d(display7segmentos_2_sd),
    .c(display7segmentos_2_sc), .dp(display7segmentos_2_dp));
  display7segmentos display7segmentos_3 (
    .a(n0_13_sinc_dec_1_q3), .b(n0_13_sinc_dec_1_q2), .c(n0_13_sinc_dec_1_q1), .d(n0_13_sinc_dec_1_q0),
    .sa(display7segmentos_3_sa), .sb(display7segmentos_3_sb), .sc(display7segmentos_3_sc),
    .sd(display7segmentos_3_sd), .se(display7segmentos_3_se), .sf(display7segmentos_3_sf),
    .sg(display7segmentos_3_sg), .dp(display7segmentos_3_dp));
  _7_Segment_Display u_7_segment_display_3 (
    .g(display7segmentos_3_sg), .f(display7segmentos_3_sf), .a(display7segmentos_3_sa),
    .b(display7segmentos_3_sb), .e(display7segmentos_3_se), .d(display7segmentos_3_sd),
    .c(display7segmentos_3_sc), .dp(display7segmentos_3_dp));
endmodule

module decre_cres_sic (
  input  UP_DOWN,
  output _1,
  output _2,
  output _3,
  output _0
);

  wire A_B_out, A_out, A_prime_B_prime_out, A_prime_out, B_C_out, B_prime_C_prime_out, clock_1_out,
       j_k_ff_1_qn, j_k_ff_2_qn, j_k_ff_3_qn, not_1_out, not_2_out, or_1_out, or_2_out, or_3_out;

  not not_1 (not_1_out, UP_DOWN);
  Clock clock_1 (.out(clock_1_out));
  and A_B (A_B_out, UP_DOWN, _1, _0);
  and A_prime_B_prime (A_prime_B_prime_out, j_k_ff_2_qn, j_k_ff_1_qn, not_1_out);
  J_K_Flip_Flop j_k_ff_1 (
    .J(1'b1), .clk(clock_1_out), .K(1'b1), .Q(_0), .Qn(j_k_ff_1_qn), .reset(not_2_out));  // open: preset, en
  not not_2 (not_2_out, 1'b1);
  or or_1 (or_1_out, A_B_out, A_prime_B_prime_out);
  J_K_Flip_Flop j_k_ff_2 (
    .J(or_2_out), .clk(clock_1_out), .K(or_2_out), .Q(_1), .Qn(j_k_ff_2_qn), .reset(not_2_out));  // open: preset, en
  and A (A_out, UP_DOWN, _0);
  and A_prime (A_prime_out, not_1_out, j_k_ff_1_qn);
  or or_2 (or_2_out, A_out, A_prime_out);
  J_K_Flip_Flop j_k_ff_3 (
    .J(or_1_out), .clk(clock_1_out), .K(or_1_out), .Q(_2), .Qn(j_k_ff_3_qn), .reset(not_2_out));  // open: preset, en
  J_K_Flip_Flop j_k_ff_4 (
    .J(or_3_out), .clk(clock_1_out), .K(or_3_out), .Q(_3), .reset(not_2_out));  // open: Qn, preset, en
  and B_C (B_C_out, _2, UP_DOWN, or_1_out);
  and B_prime_C_prime (B_prime_C_prime_out, not_1_out, j_k_ff_3_qn, or_1_out);
  or or_3 (or_3_out, B_C_out, B_prime_C_prime_out);
endmodule

module dc_cr_sinc_display (
  input  in_1
);

  wire decre_ces_sic2_1__0, decre_ces_sic2_1__1, decre_ces_sic2_1__2, decre_ces_sic2_1__3,
       decre_cres_sic_1__0, decre_cres_sic_1__1, decre_cres_sic_1__2, decre_cres_sic_1__3,
       display7segmentos_1_dp, display7segmentos_1_sa, display7segmentos_1_sb, display7segmentos_1_sc,
       display7segmentos_1_sd, display7segmentos_1_se, display7segmentos_1_sf, display7segmentos_1_sg,
       display7segmentos_2_dp, display7segmentos_2_sa, display7segmentos_2_sb, display7segmentos_2_sc,
       display7segmentos_2_sd, display7segmentos_2_se, display7segmentos_2_sf, display7segmentos_2_sg;

  decre_cres_sic decre_cres_sic_1 (
    .UP_DOWN(in_1), ._0(decre_cres_sic_1__0), ._1(decre_cres_sic_1__1), ._2(decre_cres_sic_1__2),
    ._3(decre_cres_sic_1__3));
  decre_ces_sic2 decre_ces_sic2_1 (
    ._0(decre_ces_sic2_1__0), ._1(decre_ces_sic2_1__1), ._2(decre_ces_sic2_1__2), ._3(decre_ces_sic2_1__3));
  display7segmentos display7segmentos_1 (
    .a(decre_cres_sic_1__3), .b(decre_cres_sic_1__2), .c(decre_cres_sic_1__1), .d(decre_cres_sic_1__0),
    .sa(display7segmentos_1_sa), .sb(display7segmentos_1_sb), .sc(display7segmentos_1_sc),
    .sd(display7segmentos_1_sd), .se(display7segmentos_1_se), .sf(display7segmentos_1_sf),
    .sg(display7segmentos_1_sg), .dp(display7segmentos_1_dp));
  display7segmentos display7segmentos_2 (
    .a(decre_ces_sic2_1__3), .b(decre_ces_sic2_1__2), .c(decre_ces_sic2_1__1), .d(decre_ces_sic2_1__0),
    .sa(display7segmentos_2_sa), .sb(display7segmentos_2_sb), .sc(display7segmentos_2_sc),
    .sd(display7segmentos_2_sd), .se(display7segmentos_2_se), .sf(display7segmentos_2_sf),
    .sg(display7segmentos_2_sg), .dp(display7segmentos_2_dp));
  _7_Segment_Display u_7_segment_display_1 (
    .g(display7segmentos_1_sg), .f(display7segmentos_1_sf), .a(display7segmentos_1_sa),
    .b(display7segmentos_1_sb), .e(display7segmentos_1_se), .d(display7segmentos_1_sd),
    .c(display7segmentos_1_sc), .dp(display7segmentos_1_dp));
  _7_Segment_Display u_7_segment_display_2 (
    .g(display7segmentos_2_sg), .f(display7segmentos_2_sf), .a(display7segmentos_2_sa),
    .b(display7segmentos_2_sb), .e(display7segmentos_2_se), .d(display7segmentos_2_sd),
    .c(display7segmentos_2_sc), .dp(display7segmentos_2_dp));
endmodule

module decre_ces_sic2 (
  output _1,
  output _2,
  output _3,
  output _0
);

  wire A_B_out, A_out, A_prime_B_prime_out, A_prime_out, and_1_out, and_2_out, B_C_out, B_prime_C_prime_out,
       clock_1_out, j_k_ff_1_qn, j_k_ff_2_qn, j_k_ff_3_qn, j_k_ff_4_qn, latchrs_1_q, not_1_out, not_2_out,
       or_1_out, or_2_out, or_3_out, or_4_out;

  latchRS latchrs_1 (.R(and_2_out), .C(or_1_out), .Q(latchrs_1_q));  // open: Q_prime
  or or_1 (or_1_out, and_1_out, and_2_out);
  and and_1 (and_1_out, _3, _2, _1, _0);
  not not_1 (not_1_out, latchrs_1_q);
  and and_2 (and_2_out, j_k_ff_4_qn, j_k_ff_3_qn, j_k_ff_2_qn, j_k_ff_1_qn);
  Clock clock_1 (.out(clock_1_out));
  and A_B (A_B_out, latchrs_1_q, _1, _0);
  and A_prime_B_prime (A_prime_B_prime_out, j_k_ff_2_qn, j_k_ff_1_qn, not_1_out);
  J_K_Flip_Flop j_k_ff_1 (
    .J(1'b1), .clk(clock_1_out), .K(1'b1), .Q(_0), .Qn(j_k_ff_1_qn), .reset(not_2_out));  // open: preset, en
  not not_2 (not_2_out, 1'b1);
  or or_2 (or_2_out, A_B_out, A_prime_B_prime_out);
  J_K_Flip_Flop j_k_ff_2 (
    .J(or_3_out), .clk(clock_1_out), .K(or_3_out), .Q(_1), .Qn(j_k_ff_2_qn), .reset(not_2_out));  // open: preset, en
  and A (A_out, latchrs_1_q, _0);
  and A_prime (A_prime_out, not_1_out, j_k_ff_1_qn);
  or or_3 (or_3_out, A_out, A_prime_out);
  J_K_Flip_Flop j_k_ff_3 (
    .J(or_2_out), .clk(clock_1_out), .K(or_2_out), .Q(_2), .Qn(j_k_ff_3_qn), .reset(not_2_out));  // open: preset, en
  J_K_Flip_Flop j_k_ff_4 (
    .J(or_4_out), .clk(clock_1_out), .K(or_4_out), .Q(_3), .Qn(j_k_ff_4_qn), .reset(not_2_out));  // open: preset, en
  and B_C (B_C_out, _2, latchrs_1_q, or_2_out);
  and B_prime_C_prime (B_prime_C_prime_out, not_1_out, j_k_ff_3_qn, or_2_out);
  or or_4 (or_4_out, B_C_out, B_prime_C_prime_out);
endmodule

module latchRS (
  input  R,
  input  C,
  output Q,
  output Q_prime
);

  wire and_1_out, and_2_out, not_1_out;

  not not_1 (not_1_out, R);
  and and_1 (and_1_out, not_1_out, C);
  and and_2 (and_2_out, C, R);
  nor nor_1 (Q, and_1_out, Q_prime);
  nor nor_2 (Q_prime, Q, and_2_out);
endmodule

module SINC_0_17_6 (
  input  INICIO,
  input  A0,
  input  A1,
  input  A2,
  input  A4,
  input  A3,
  output out_7,
  output out_8,
  output out_9,
  output out_10,
  output out_11
);

  wire and_1_out, and_2_out, and_3_out, and_4_out, clock_1_out, flipflop_inicia_1_clear,
       flipflop_inicia_1_preset, flipflop_inicia_2_clear, flipflop_inicia_2_preset, flipflop_inicia_3_clear,
       flipflop_inicia_3_preset, flipflop_inicia_4_clear, flipflop_inicia_4_preset, flipflop_inicia_5_clear,
       flipflop_inicia_5_preset, j_k_ff_1_qn, j_k_ff_3_qn, not_1_out, not_2_out, or_1_out, or_2_out,
       or_3_out, or_4_out, or_5_out;

  Clock clock_1 (.out(clock_1_out));
  flipflop_inicia flipflop_inicia_1 (
    .A(A0), .INICIO(INICIO), .preset(flipflop_inicia_1_preset), .clear(flipflop_inicia_1_clear));
  J_K_Flip_Flop j_k_ff_1 (
    .J(1'b1), .clk(clock_1_out), .K(1'b1), .Q(out_8), .Qn(j_k_ff_1_qn), .preset(flipflop_inicia_1_preset),
    .reset(or_1_out));  // open: en
  or or_1 (or_1_out, not_2_out, flipflop_inicia_1_clear);
  flipflop_inicia flipflop_inicia_2 (
    .A(A1), .INICIO(INICIO), .preset(flipflop_inicia_2_preset), .clear(flipflop_inicia_2_clear));
  J_K_Flip_Flop j_k_ff_2 (
    .J(out_8), .clk(clock_1_out), .K(out_8), .Q(out_9), .preset(flipflop_inicia_2_preset), .reset(or_2_out));  // open: Qn, en
  or or_2 (or_2_out, not_2_out, flipflop_inicia_2_clear);
  and and_1 (and_1_out, out_8, out_9);
  flipflop_inicia flipflop_inicia_3 (
    .A(A2), .INICIO(INICIO), .preset(flipflop_inicia_3_preset), .clear(flipflop_inicia_3_clear));
  J_K_Flip_Flop j_k_ff_3 (
    .J(and_1_out), .clk(clock_1_out), .K(and_1_out), .Q(out_10), .Qn(j_k_ff_3_qn),
    .preset(flipflop_inicia_3_preset), .reset(or_3_out));  // open: en
  or or_3 (or_3_out, not_2_out, flipflop_inicia_3_clear);
  flipflop_inicia flipflop_inicia_4 (
    .A(A3), .INICIO(INICIO), .preset(flipflop_inicia_4_preset), .clear(flipflop_inicia_4_clear));
  and and_2 (and_2_out, and_1_out, out_10);
  or or_4 (or_4_out, not_2_out, flipflop_inicia_4_clear);
  J_K_Flip_Flop j_k_ff_4 (
    .J(and_2_out), .clk(clock_1_out), .K(and_2_out), .Q(out_11), .preset(flipflop_inicia_4_preset),
    .reset(or_4_out));  // open: Qn, en
  flipflop_inicia flipflop_inicia_5 (
    .A(A4), .INICIO(INICIO), .preset(flipflop_inicia_5_preset), .clear(flipflop_inicia_5_clear));
  and and_3 (and_3_out, and_2_out, out_11);
  J_K_Flip_Flop j_k_ff_5 (
    .J(and_3_out), .clk(clock_1_out), .K(and_3_out), .Q(out_7), .preset(flipflop_inicia_5_preset),
    .reset(or_5_out));  // open: Qn, en
  or or_5 (or_5_out, not_2_out, flipflop_inicia_5_clear);
  and and_4 (and_4_out, out_7, j_k_ff_3_qn, out_9, j_k_ff_1_qn);
  not not_1 (not_1_out, and_4_out);
  not not_2 (not_2_out, not_1_out);
endmodule

module atividade05_10DISPLAY (
  input  UP_DOWN,
  input  PAUSAR
);

  wire A0, A1, A2, A3, B0, B1, B2, B3, C0, C1, C2, C3, clock_1_out, CN1, CN2, CN3, D0, D1, D2, D3,
       display7segmentos_1_dp, display7segmentos_1_sa, display7segmentos_1_sb, display7segmentos_1_sc,
       display7segmentos_1_sd, display7segmentos_1_se, display7segmentos_1_sf, display7segmentos_1_sg,
       display7segmentos_2_dp, display7segmentos_2_sa, display7segmentos_2_sb, display7segmentos_2_sc,
       display7segmentos_2_sd, display7segmentos_2_se, display7segmentos_2_sf, display7segmentos_2_sg,
       display7segmentos_3_dp, display7segmentos_3_sa, display7segmentos_3_sb, display7segmentos_3_sc,
       display7segmentos_3_sd, display7segmentos_3_se, display7segmentos_3_sf, display7segmentos_3_sg,
       display7segmentos_4_dp, display7segmentos_4_sa, display7segmentos_4_sb, display7segmentos_4_sc,
       display7segmentos_4_sd, display7segmentos_4_se, display7segmentos_4_sf, display7segmentos_4_sg, R;

  display7segmentos display7segmentos_1 (
    .a(D3), .b(D2), .c(D1), .d(D0), .sa(display7segmentos_1_sa), .sb(display7segmentos_1_sb),
    .sc(display7segmentos_1_sc), .sd(display7segmentos_1_sd), .se(display7segmentos_1_se),
    .sf(display7segmentos_1_sf), .sg(display7segmentos_1_sg), .dp(display7segmentos_1_dp));
  Clock clock_1 (.out(clock_1_out));
  _7_Segment_Display u_7_segment_display_1 (
    .g(display7segmentos_1_sg), .f(display7segmentos_1_sf), .a(display7segmentos_1_sa),
    .b(display7segmentos_1_sb), .e(display7segmentos_1_se), .d(display7segmentos_1_sd),
    .c(display7segmentos_1_sc), .dp(display7segmentos_1_dp));
  atividade05_10 atividade05_10_1 (
    .UP_DOWN(UP_DOWN), .clock(clock_1_out), .PAUSAR(PAUSAR), .resetar(R), ._0(A0), ._1(A1), ._2(A2), ._3(A3),
    .conector(CN1));
  atividade05_10 atividade05_10_2 (
    .UP_DOWN(UP_DOWN), .clock(CN1), .PAUSAR(PAUSAR), .resetar(R), ._0(B0), ._1(B1), ._2(B2), ._3(B3),
    .conector(CN2));
  display7segmentos display7segmentos_2 (
    .a(C3), .b(C2), .c(C1), .d(C0), .sa(display7segmentos_2_sa), .sb(display7segmentos_2_sb),
    .sc(display7segmentos_2_sc), .sd(display7segmentos_2_sd), .se(display7segmentos_2_se),
    .sf(display7segmentos_2_sf), .sg(display7segmentos_2_sg), .dp(display7segmentos_2_dp));
  Button RESETAR (.out(R));
  atividade05_10 atividade05_10_3 (
    .UP_DOWN(UP_DOWN), .clock(CN2), .PAUSAR(PAUSAR), .resetar(R), ._0(C0), ._1(C1), ._2(C2), ._3(C3),
    .conector(CN3));
  _7_Segment_Display u_7_segment_display_2 (
    .g(display7segmentos_2_sg), .f(display7segmentos_2_sf), .a(display7segmentos_2_sa),
    .b(display7segmentos_2_sb), .e(display7segmentos_2_se), .d(display7segmentos_2_sd),
    .c(display7segmentos_2_sc), .dp(display7segmentos_2_dp));
  LED led_1 (.in(D2));
  LED led_2 (.in(D3));
  atividade05_10 atividade05_10_4 (
    .UP_DOWN(UP_DOWN), .clock(CN3), .PAUSAR(PAUSAR), .resetar(R), ._0(D0), ._1(D1), ._2(D2), ._3(D3));  // open: conector
  LED led_3 (.in(D0));
  LED led_4 (.in(D1));
  display7segmentos display7segmentos_3 (
    .a(B3), .b(B2), .c(B1), .d(B0), .sa(display7segmentos_3_sa), .sb(display7segmentos_3_sb),
    .sc(display7segmentos_3_sc), .sd(display7segmentos_3_sd), .se(display7segmentos_3_se),
    .sf(display7segmentos_3_sf), .sg(display7segmentos_3_sg), .dp(display7segmentos_3_dp));
  LED led_5 (.in(C3));
  LED led_6 (.in(C2));
  LED led_7 (.in(C0));
  LED led_8 (.in(C1));
  _7_Segment_Display u_7_segment_display_3 (
    .g(display7segmentos_3_sg), .f(display7segmentos_3_sf), .a(display7segmentos_3_sa),
    .b(display7segmentos_3_sb), .e(display7segmentos_3_se), .d(display7segmentos_3_sd),
    .c(display7segmentos_3_sc), .dp(display7segmentos_3_dp));
  LED led_9 (.in(B3));
  LED led_10 (.in(B2));
  LED led_11 (.in(B1));
  LED led_12 (.in(B0));
  display7segmentos display7segmentos_4 (
    .a(A3), .b(A2), .c(A1), .d(A0), .sa(display7segmentos_4_sa), .sb(display7segmentos_4_sb),
    .sc(display7segmentos_4_sc), .sd(display7segmentos_4_sd), .se(display7segmentos_4_se),
    .sf(display7segmentos_4_sf), .sg(display7segmentos_4_sg), .dp(display7segmentos_4_dp));
  LED led_13 (.in(A2));
  LED led_14 (.in(A3));
  LED led_15 (.in(A1));
  _7_Segment_Display u_7_segment_display_4 (
    .g(display7segmentos_4_sg), .f(display7segmentos_4_sf), .a(display7segmentos_4_sa),
    .b(display7segmentos_4_sb), .e(display7segmentos_4_se), .d(display7segmentos_4_sd),
    .c(display7segmentos_4_sc), .dp(display7segmentos_4_dp));
  LED led_16 (.in(A0));

  // Other names for the same wires on the sheet: P = PAUSAR; U_D = UP_DOWN
endmodule

module atividade05_10 (
  input  UP_DOWN,
  input  clock,
  input  PAUSAR,
  input  resetar,
  output _1,
  output _2,
  output _3,
  output _0,
  output conector
);

  wire A_B_out, A_out, A_prime_B_prime_out, A_prime_out, and_1_out, and_2_out, B_C_out, B_prime_C_prime_out,
       C1, c1_t, C2, c2_t, C3, c3_t, C4, c4_t, F0, F1, F2, F3, flipflop_inicia_1_preset,
       flipflop_inicia_2_preset, flipflop_inicia_3_preset, flipflop_inicia_4_preset, INICIO_out, j_k_ff_1_qn,
       j_k_ff_2_qn, j_k_ff_3_qn, not_1_out, not_2_out, not_3_out, not_4_out, not_5_out, or_1_out, or_2_out,
       or_3_out, or_9_out, or_10_out, or_11_out, or_12_out, p1, p2, p3, p4;

  not not_1 (not_1_out, UP_DOWN);
  not not_2 (not_2_out, UP_DOWN);
  and and_1 (and_1_out, clock, not_3_out);
  not not_3 (not_3_out, PAUSAR);
  and A_B (A_B_out, UP_DOWN, _1, _0);
  and A_prime_B_prime (A_prime_B_prime_out, j_k_ff_2_qn, j_k_ff_1_qn, not_1_out);
  J_K_Flip_Flop j_k_ff_1 (
    .J(1'b1), .clk(and_1_out), .K(1'b1), .Q(_0), .Qn(j_k_ff_1_qn), .preset(or_10_out), .reset(C1));  // open: en
  or or_1 (or_1_out, A_B_out, A_prime_B_prime_out);
  J_K_Flip_Flop j_k_ff_2 (
    .J(or_2_out), .clk(and_1_out), .K(or_2_out), .Q(_1), .Qn(j_k_ff_2_qn), .preset(or_9_out), .reset(C2));  // open: en
  and INICIO (INICIO_out, _3, _2, _1, _0, not_2_out);
  and A (A_out, UP_DOWN, _0);
  and A_prime (A_prime_out, not_1_out, j_k_ff_1_qn);
  or or_2 (or_2_out, A_out, A_prime_out);
  J_K_Flip_Flop j_k_ff_3 (
    .J(or_1_out), .clk(and_1_out), .K(or_1_out), .Q(_2), .Qn(j_k_ff_3_qn), .preset(or_11_out), .reset(C3));  // open: en
  J_K_Flip_Flop j_k_ff_4 (
    .J(or_3_out), .clk(and_1_out), .K(or_3_out), .Q(_3), .preset(or_12_out), .reset(C4));  // open: Qn, en
  and B_C (B_C_out, _2, UP_DOWN, or_1_out);
  and B_prime_C_prime (B_prime_C_prime_out, not_1_out, j_k_ff_3_qn, or_1_out);
  and and_2 (and_2_out, _3, j_k_ff_3_qn, _1, j_k_ff_1_qn);
  or or_3 (or_3_out, B_C_out, B_prime_C_prime_out);
  or or_4 (C2, not_4_out, c2_t, F1);
  or or_5 (C3, not_4_out, c3_t, F2);
  or or_6 (C1, not_4_out, c1_t, F0);
  not not_4 (not_4_out, not_5_out);
  not not_5 (not_5_out, and_2_out);
  componente_resetar componente_resetar_1 (
    .up_down(not_2_out), .INICIO(resetar), .P1(p1), .C1(c1_t), .P2(p2), .C2(c2_t), .P3(p3), .C3(c3_t),
    .P4(p4), .C4(c4_t));
  or or_7 (C4, not_4_out, c4_t, F3);
  or or_8 (conector, not_4_out, INICIO_out);
  or or_9 (or_9_out, flipflop_inicia_1_preset, p2);
  or or_10 (or_10_out, flipflop_inicia_2_preset, p1);
  flipflop_inicia flipflop_inicia_1 (.A(1'b0), .INICIO(INICIO_out), .preset(flipflop_inicia_1_preset), .clear(F1));
  flipflop_inicia flipflop_inicia_2 (.A(1'b1), .INICIO(INICIO_out), .preset(flipflop_inicia_2_preset), .clear(F0));
  or or_11 (or_11_out, flipflop_inicia_3_preset, p3);
  flipflop_inicia flipflop_inicia_3 (.A(1'b0), .INICIO(INICIO_out), .preset(flipflop_inicia_3_preset), .clear(F2));
  or or_12 (or_12_out, flipflop_inicia_4_preset, p4);
  flipflop_inicia flipflop_inicia_4 (.A(1'b1), .INICIO(INICIO_out), .preset(flipflop_inicia_4_preset), .clear(F3));
endmodule

module componente_resetar (
  input  up_down,
  input  INICIO,
  output P1,
  output C1,
  output P2,
  output C2,
  output P3,
  output C3,
  output P4,
  output C4
);

  wire nand_1_out, nand_2_out, not_1_out;

  not not_1 (not_1_out, up_down);
  flipflop_inicia flipflop_inicia_1 (.A(1'b0), .INICIO(INICIO), .preset(P2), .clear(C2));
  flipflop_inicia flipflop_inicia_2 (.A(nand_1_out), .INICIO(INICIO), .preset(P1), .clear(C1));
  nand nand_1 (nand_1_out, not_1_out, not_1_out);
  flipflop_inicia flipflop_inicia_3 (.A(1'b0), .INICIO(INICIO), .preset(P3), .clear(C3));
  flipflop_inicia flipflop_inicia_4 (.A(nand_2_out), .INICIO(INICIO), .preset(P4), .clear(C4));
  nand nand_2 (nand_2_out, not_1_out, not_1_out);
endmodule

module teste_reset (
);

  atividade05_10 atividade05_10_1 ();  // open: UP_DOWN, clock, PAUSAR, resetar, _0, _1, _2, _3, conector
endmodule

module mudanca_niveis (
  input  E,
  output S
);

  wire and_1_out, and_2_out, and_3_out, and_4_out, and_5_out, and_6_out, and_7_out, and_8_out, and_9_out,
       and_10_out, clock_1_out, D0_q, not_1_out, not_2_out, not_3_out, not_4_out, not_5_out, not_6_out,
       not_7_out, not_8_out, not_9_out, not_10_out, not_11_out, not_12_out, not_13_out, or_2_out, or_3_out,
       Q1_q;

  Clock clock_1 (.out(clock_1_out));
  or or_1 (S, and_1_out, and_2_out);
  and and_1 (and_1_out, Q1_q, D0_q);
  D_Flip_Flop Q1 (.clk(clock_1_out), .D(or_2_out), .Q(Q1_q));  // open: Qn, preset, en, reset
  D_Flip_Flop D0 (.clk(clock_1_out), .D(or_3_out), .Q(D0_q));  // open: Qn, preset, en, reset
  and and_2 (and_2_out, not_1_out, D0_q);
  not not_1 (not_1_out, Q1_q);
  not not_2 (not_2_out, Q1_q);
  not not_3 (not_3_out, D0_q);
  and and_3 (and_3_out, not_3_out, Q1_q, E);
  and and_4 (and_4_out, D0_q, not_2_out, E);
  not not_4 (not_4_out, E);
  not not_5 (not_5_out, D0_q);
  and and_5 (and_5_out, not_5_out, Q1_q, not_4_out);
  or or_2 (or_2_out, and_3_out, and_4_out, and_5_out, and_6_out);
  not not_6 (not_6_out, E);
  not not_7 (not_7_out, Q1_q);
  and and_6 (and_6_out, D0_q, not_7_out, not_6_out);
  not not_8 (not_8_out, Q1_q);
  not not_9 (not_9_out, Q1_q);
  not not_10 (not_10_out, D0_q);
  not not_11 (not_11_out, E);
  and and_7 (and_7_out, not_10_out, not_8_out, E);
  and and_8 (and_8_out, D0_q, not_9_out, not_11_out);
  not not_12 (not_12_out, D0_q);
  not not_13 (not_13_out, E);
  and and_9 (and_9_out, not_12_out, Q1_q, not_13_out);
  or or_3 (or_3_out, and_7_out, and_8_out, and_9_out, and_10_out);
  and and_10 (and_10_out, D0_q, Q1_q, E);
endmodule

module mudanca_contador (
  input  E
);

  wire contador_assincrono_1_s0, contador_assincrono_1_s1, contador_assincrono_1_s2,
       contador_assincrono_1_s3, display7segmentos_1_dp, display7segmentos_1_sa, display7segmentos_1_sb,
       display7segmentos_1_sc, display7segmentos_1_sd, display7segmentos_1_se, display7segmentos_1_sf,
       display7segmentos_1_sg, mudanca_niveis_1_s;

  mudanca_niveis mudanca_niveis_1 (.S(mudanca_niveis_1_s), .E(E));
  contador_assincrono contador_assincrono_1 (
    .in_1(mudanca_niveis_1_s), .s0(contador_assincrono_1_s0), .s1(contador_assincrono_1_s1),
    .s2(contador_assincrono_1_s2), .s3(contador_assincrono_1_s3));
  display7segmentos display7segmentos_1 (
    .a(contador_assincrono_1_s3), .b(contador_assincrono_1_s2), .c(contador_assincrono_1_s1),
    .d(contador_assincrono_1_s0), .sa(display7segmentos_1_sa), .sb(display7segmentos_1_sb),
    .sc(display7segmentos_1_sc), .sd(display7segmentos_1_sd), .se(display7segmentos_1_se),
    .sf(display7segmentos_1_sf), .sg(display7segmentos_1_sg), .dp(display7segmentos_1_dp));
  _7_Segment_Display u_7_segment_display_1 (
    .g(display7segmentos_1_sg), .f(display7segmentos_1_sf), .a(display7segmentos_1_sa),
    .b(display7segmentos_1_sb), .e(display7segmentos_1_se), .d(display7segmentos_1_sd),
    .c(display7segmentos_1_sc), .dp(display7segmentos_1_dp));
endmodule

module ex1 (
  input  E,
  input  in_2,
  output S
);

  wire and_2_out, and_3_out, and_4_out, and_5_out, and_6_out, FF0_q, FF1_q, not_1_out, not_2_out, not_3_out,
       not_4_out, not_5_out, not_6_out, or_1_out, or_2_out;

  and and_1 (S, FF1_q, FF0_q);
  D_Flip_Flop FF1 (.clk(in_2), .D(or_1_out), .Q(FF1_q));  // open: Qn, preset, en, reset
  D_Flip_Flop FF0 (.clk(in_2), .D(or_2_out), .Q(FF0_q));  // open: Qn, preset, en, reset
  not not_1 (not_1_out, FF0_q);
  and and_2 (and_2_out, not_1_out, FF1_q, E);
  not not_2 (not_2_out, FF1_q);
  not not_3 (not_3_out, E);
  and and_3 (and_3_out, not_2_out, FF0_q, not_3_out);
  or or_1 (or_1_out, and_2_out, and_3_out);
  not not_4 (not_4_out, FF0_q);
  not not_5 (not_5_out, FF1_q);
  and and_4 (and_4_out, not_5_out, not_4_out, E);
  not not_6 (not_6_out, FF0_q);
  and and_5 (and_5_out, FF0_q, FF1_q, E);
  and and_6 (and_6_out, not_6_out, FF1_q, E);
  or or_2 (or_2_out, and_4_out, and_6_out, and_5_out);
endmodule

module ex1_7seg (
  input  E
);

  wire clock_1_out, contador_assincrono_1_s0, contador_assincrono_1_s1, contador_assincrono_1_s2,
       contador_assincrono_1_s3, display7segmentos_1_dp, display7segmentos_1_sa, display7segmentos_1_sb,
       display7segmentos_1_sc, display7segmentos_1_sd, display7segmentos_1_se, display7segmentos_1_sf,
       display7segmentos_1_sg, ex1_1_s;

  ex1 ex1_1 (.in_2(clock_1_out), .S(ex1_1_s), .E(E));
  contador_assincrono contador_assincrono_1 (
    .in_1(ex1_1_s), .s0(contador_assincrono_1_s0), .s1(contador_assincrono_1_s1),
    .s2(contador_assincrono_1_s2), .s3(contador_assincrono_1_s3));
  Clock clock_1 (.out(clock_1_out));
  display7segmentos display7segmentos_1 (
    .a(contador_assincrono_1_s3), .b(contador_assincrono_1_s2), .c(contador_assincrono_1_s1),
    .d(contador_assincrono_1_s0), .sa(display7segmentos_1_sa), .sb(display7segmentos_1_sb),
    .sc(display7segmentos_1_sc), .sd(display7segmentos_1_sd), .se(display7segmentos_1_se),
    .sf(display7segmentos_1_sf), .sg(display7segmentos_1_sg), .dp(display7segmentos_1_dp));
  _7_Segment_Display u_7_segment_display_1 (
    .g(display7segmentos_1_sg), .f(display7segmentos_1_sf), .a(display7segmentos_1_sa),
    .b(display7segmentos_1_sb), .e(display7segmentos_1_se), .d(display7segmentos_1_sd),
    .c(display7segmentos_1_sc), .dp(display7segmentos_1_dp));
endmodule

module impares (
  output Q0,
  output Q1,
  output Q2,
  output Q3
);

  wire and_1_out, and_2_out, and_3_out, and_4_out, and_5_out, and_6_out, and_7_out, and_8_out, and_9_out,
       and_10_out, and_11_out, and_12_out, clock_1_out, D1_out, D2_out, D3_out, not_1_out, not_2_out,
       not_3_out, not_4_out, not_5_out, not_6_out, not_7_out, not_8_out, not_9_out, not_10_out, not_11_out,
       not_12_out, not_13_out, not_14_out, not_15_out, not_16_out, not_17_out, not_18_out, not_19_out;

  Clock clock_1 (.out(clock_1_out));
  D_Flip_Flop u_Q3 (.clk(clock_1_out), .D(D3_out), .Q(Q3));  // open: Qn, preset, en, reset
  D_Flip_Flop u_Q2 (.clk(clock_1_out), .D(D2_out), .Q(Q2));  // open: Qn, preset, en, reset
  D_Flip_Flop u_Q1 (.clk(clock_1_out), .D(D1_out), .Q(Q1));  // open: Qn, preset, en, reset
  D_Flip_Flop u_Q0 (.clk(clock_1_out), .D(1'b1), .Q(Q0));  // open: Qn, preset, en, reset
  not not_1 (not_1_out, Q3);
  and and_1 (and_1_out, not_1_out, Q2, Q1, Q0);
  not not_2 (not_2_out, Q2);
  not not_3 (not_3_out, Q3);
  not not_4 (not_4_out, Q1);
  and and_2 (and_2_out, not_3_out, not_2_out, not_4_out, Q0);
  not not_5 (not_5_out, Q2);
  and and_3 (and_3_out, Q3, not_5_out, not_7_out, Q0);
  not not_6 (not_6_out, Q3);
  and and_4 (and_4_out, not_6_out, Q2, not_9_out, Q0);
  not not_7 (not_7_out, Q1);
  not not_8 (not_8_out, Q2);
  or D3 (D3_out, and_1_out, and_3_out, and_5_out, and_7_out);
  not not_9 (not_9_out, Q1);
  not not_10 (not_10_out, Q2);
  or D1 (D1_out, and_2_out, and_4_out, and_6_out, and_8_out);
  and and_5 (and_5_out, Q3, not_8_out, Q1, Q0);
  not not_11 (not_11_out, Q1);
  and and_6 (and_6_out, Q3, not_10_out, not_11_out, Q0);
  not not_12 (not_12_out, Q1);
  and and_7 (and_7_out, Q3, Q2, not_12_out, Q0);
  not not_13 (not_13_out, Q1);
  and and_8 (and_8_out, Q3, Q2, not_13_out, Q0);
  not not_14 (not_14_out, Q3);
  not not_15 (not_15_out, Q2);
  and and_9 (and_9_out, not_14_out, not_15_out, Q1, Q0);
  not not_16 (not_16_out, Q1);
  not not_17 (not_17_out, Q3);
  and and_10 (and_10_out, not_17_out, Q2, not_16_out, Q0);
  not not_18 (not_18_out, Q2);
  and and_11 (and_11_out, Q3, not_18_out, Q1, Q0);
  or D2 (D2_out, and_9_out, and_10_out, and_11_out, and_12_out);
  not not_19 (not_19_out, Q1);
  and and_12 (and_12_out, Q3, Q2, not_19_out, Q0);
endmodule

module impares_7seg (
);

  wire display7segmentos_1_dp, display7segmentos_1_sa, display7segmentos_1_sb, display7segmentos_1_sc,
       display7segmentos_1_sd, display7segmentos_1_se, display7segmentos_1_sf, display7segmentos_1_sg,
       impares_1_q0, impares_1_q1, impares_1_q2, impares_1_q3;

  impares impares_1 (.Q0(impares_1_q0), .Q1(impares_1_q1), .Q2(impares_1_q2), .Q3(impares_1_q3));
  display7segmentos display7segmentos_1 (
    .a(impares_1_q3), .b(impares_1_q2), .c(impares_1_q1), .d(impares_1_q0), .sa(display7segmentos_1_sa),
    .sb(display7segmentos_1_sb), .sc(display7segmentos_1_sc), .sd(display7segmentos_1_sd),
    .se(display7segmentos_1_se), .sf(display7segmentos_1_sf), .sg(display7segmentos_1_sg),
    .dp(display7segmentos_1_dp));
  _7_Segment_Display u_7_segment_display_1 (
    .g(display7segmentos_1_sg), .f(display7segmentos_1_sf), .a(display7segmentos_1_sa),
    .b(display7segmentos_1_sb), .e(display7segmentos_1_se), .d(display7segmentos_1_sd),
    .c(display7segmentos_1_sc), .dp(display7segmentos_1_dp));
endmodule

module pares (
  output Q0,
  output Q1,
  output Q2,
  output Q3
);

  wire and_1_out, and_2_out, and_3_out, and_4_out, and_5_out, and_6_out, and_7_out, and_8_out, and_9_out,
       and_10_out, and_11_out, and_12_out, clock_1_out, D1_out, D2_out, D3_out, not_1_out, not_2_out,
       not_3_out, not_4_out, not_5_out, not_6_out, not_7_out, not_8_out, not_9_out, not_10_out, not_11_out,
       not_12_out, not_13_out, not_14_out, not_15_out, not_16_out, not_17_out, not_18_out, not_19_out,
       not_20_out, not_21_out, not_22_out, not_23_out, not_24_out, not_25_out, not_26_out, not_27_out,
       not_28_out, not_29_out, not_30_out, not_31_out;

  Clock clock_1 (.out(clock_1_out));
  D_Flip_Flop u_Q3 (.clk(clock_1_out), .D(D3_out), .Q(Q3));  // open: Qn, preset, en, reset
  D_Flip_Flop u_Q2 (.clk(clock_1_out), .D(D2_out), .Q(Q2));  // open: Qn, preset, en, reset
  D_Flip_Flop u_Q1 (.clk(clock_1_out), .D(D1_out), .Q(Q1));  // open: Qn, preset, en, reset
  D_Flip_Flop u_Q0 (.clk(clock_1_out), .D(1'b0), .Q(Q0));  // open: Qn, preset, en, reset
  not not_1 (not_1_out, Q3);
  and and_1 (and_1_out, not_1_out, Q2, Q1, not_5_out);
  not not_2 (not_2_out, Q1);
  not not_3 (not_3_out, Q3);
  not not_4 (not_4_out, Q2);
  and and_2 (and_2_out, not_3_out, not_4_out, not_2_out, not_7_out);
  not not_5 (not_5_out, Q0);
  not not_6 (not_6_out, Q2);
  and and_3 (and_3_out, Q3, not_6_out, not_11_out, not_10_out);
  not not_7 (not_7_out, Q0);
  not not_8 (not_8_out, Q3);
  and and_4 (and_4_out, not_8_out, Q2, not_14_out, not_12_out);
  not not_9 (not_9_out, Q2);
  not not_10 (not_10_out, Q0);
  not not_11 (not_11_out, Q1);
  or D3 (D3_out, and_1_out, and_3_out, and_5_out, and_7_out);
  not not_12 (not_12_out, Q0);
  not not_13 (not_13_out, Q2);
  not not_14 (not_14_out, Q1);
  or D1 (D1_out, and_2_out, and_4_out, and_6_out, and_8_out);
  not not_15 (not_15_out, Q0);
  and and_5 (and_5_out, Q3, not_9_out, Q1, not_15_out);
  not not_16 (not_16_out, Q0);
  not not_17 (not_17_out, Q1);
  and and_6 (and_6_out, Q3, not_13_out, not_17_out, not_16_out);
  not not_18 (not_18_out, Q0);
  not not_19 (not_19_out, Q1);
  and and_7 (and_7_out, Q3, Q2, not_19_out, not_18_out);
  not not_20 (not_20_out, Q0);
  not not_21 (not_21_out, Q1);
  and and_8 (and_8_out, Q3, Q2, not_21_out, not_20_out);
  not not_22 (not_22_out, Q2);
  not not_23 (not_23_out, Q3);
  not not_24 (not_24_out, Q0);
  and and_9 (and_9_out, not_23_out, not_22_out, Q1, not_24_out);
  not not_25 (not_25_out, Q1);
  not not_26 (not_26_out, Q3);
  and and_10 (and_10_out, not_26_out, Q2, not_25_out, not_27_out);
  not not_27 (not_27_out, Q0);
  not not_28 (not_28_out, Q2);
  and and_11 (and_11_out, Q3, not_28_out, Q1, not_29_out);
  or D2 (D2_out, and_9_out, and_10_out, and_11_out, and_12_out);
  not not_29 (not_29_out, Q0);
  not not_30 (not_30_out, Q1);
  not not_31 (not_31_out, Q0);
  and and_12 (and_12_out, Q3, Q2, not_30_out, not_31_out);
endmodule

module pares_7seg (
);

  wire display7segmentos_1_dp, display7segmentos_1_sa, display7segmentos_1_sb, display7segmentos_1_sc,
       display7segmentos_1_sd, display7segmentos_1_se, display7segmentos_1_sf, display7segmentos_1_sg,
       pares_1_q0, pares_1_q1, pares_1_q2, pares_1_q3;

  pares pares_1 (.Q0(pares_1_q0), .Q1(pares_1_q1), .Q2(pares_1_q2), .Q3(pares_1_q3));
  display7segmentos display7segmentos_1 (
    .a(pares_1_q3), .b(pares_1_q2), .c(pares_1_q1), .d(pares_1_q0), .sa(display7segmentos_1_sa),
    .sb(display7segmentos_1_sb), .sc(display7segmentos_1_sc), .sd(display7segmentos_1_sd),
    .se(display7segmentos_1_se), .sf(display7segmentos_1_sf), .sg(display7segmentos_1_sg),
    .dp(display7segmentos_1_dp));
  _7_Segment_Display u_7_segment_display_1 (
    .g(display7segmentos_1_sg), .f(display7segmentos_1_sf), .a(display7segmentos_1_sa),
    .b(display7segmentos_1_sb), .e(display7segmentos_1_se), .d(display7segmentos_1_sd),
    .c(display7segmentos_1_sc), .dp(display7segmentos_1_dp));
endmodule

module exercicioMEALEY1 (
  input  E,
  input  clock,
  output s
);

  wire D0_out, D1_out, Q0_prime_Q1_prime_E_prime_2_out, Q0_prime_Q1_prime_E_prime_out, Q0_prime_Q1E_out,
       Q0_q, Q0Q1_prime_E_prime_2_out, Q0Q1_prime_E_prime_3_out, Q0Q1_prime_E_prime_out, Q1_q;

  D_Flip_Flop Q1 (.clk(clock), .D(D1_out), .Q(Q1_q));  // open: Qn, preset, en, reset
  D_Flip_Flop Q0 (.clk(clock), .D(D0_out), .Q(Q0_q));  // open: Qn, preset, en, reset
  and and_1 (s, Q1_q, Q0_q, ~E);  // AND_Gate
  and Q0_prime_Q1E (Q0_prime_Q1E_out, ~Q0_q, Q1_q, E);  // AND_Gate
  and Q0Q1_prime_E_prime (Q0Q1_prime_E_prime_out, Q0_q, ~Q1_q, ~E);  // AND_Gate
  or D0 (D0_out, Q0_prime_Q1E_out, Q0Q1_prime_E_prime_out, Q0_prime_Q1_prime_E_prime_out);
  and Q0_prime_Q1_prime_E_prime (Q0_prime_Q1_prime_E_prime_out, Q0_q, Q1_q, E);
  and Q0_prime_Q1_prime_E_prime_2 (Q0_prime_Q1_prime_E_prime_2_out, ~Q0_q, ~Q1_q, ~E);  // AND_Gate
  and Q0Q1_prime_E_prime_2 (Q0Q1_prime_E_prime_2_out, Q0_q, ~Q1_q, ~E);  // AND_Gate
  and Q0Q1_prime_E_prime_3 (Q0Q1_prime_E_prime_3_out, Q0_q, Q1_q, ~E);  // AND_Gate
  or D1 (D1_out, Q0_prime_Q1_prime_E_prime_2_out, Q0Q1_prime_E_prime_2_out, Q0Q1_prime_E_prime_3_out);
endmodule

module exMEALEY2 (
  input  E,
  output S
);

  wire and_1_out, and_2_out, and_3_out, clock_1_out, or_2_out, Q0_q, Q1_prime_Q0_prime_E_out,
       Q1_prime_Q0E_out, Q1_q, Q1Q0_prime_E_out;

  Clock clock_1 (.out(clock_1_out));
  and and_1 (and_1_out, ~Q1_q, ~Q0_q, E);  // AND_Gate
  D_Flip_Flop Q1 (.clk(clock_1_out), .D(or_2_out), .Q(Q1_q));  // open: Qn, preset, en, reset
  D_Flip_Flop Q0 (.clk(clock_1_out), .D(Q1_prime_Q0_prime_E_out), .Q(Q0_q));  // open: Qn, preset, en, reset
  or or_1 (S, and_1_out, and_2_out, and_3_out);
  and and_2 (and_2_out, ~Q1_q, Q0_q, ~E);  // AND_Gate
  and and_3 (and_3_out, Q1_q, ~Q0_q, ~E);  // AND_Gate
  and Q1_prime_Q0_prime_E (Q1_prime_Q0_prime_E_out, ~Q1_q, ~Q0_q, E);  // AND_Gate
  and Q1_prime_Q0E (Q1_prime_Q0E_out, ~Q1_q, Q0_q, E);  // AND_Gate
  or or_2 (or_2_out, Q1_prime_Q0E_out, Q1Q0_prime_E_out);
  and Q1Q0_prime_E (Q1Q0_prime_E_out, Q1_q, ~Q0_q, E);  // AND_Gate
endmodule

module exMEALEY3 (
  output S3,
  output S2,
  output S1,
  output S0
);

  wire clock_1_out, D0, D1, D2, Q0, Q1, Q2, Q2_prime_Q1_prime_Q0_2_out, Q2_prime_Q1_prime_Q0_3_out,
       Q2_prime_Q1_prime_Q0_out, Q2_prime_Q1Q0_2_out, Q2_prime_Q1Q0_3_out, Q2_prime_Q1Q0_out,
       Q2_prime_Q1Q0_prime_2_out, Q2_prime_Q1Q0_prime_3_out, Q2_prime_Q1Q0_prime_out, Q2Q1_prime_Q0_2_out,
       Q2Q1_prime_Q0_3_out, Q2Q1_prime_Q0_out, Q2Q1_prime_Q0_prime_2_out, Q2Q1_prime_Q0_prime_3_out,
       Q2Q1_prime_Q0_prime_4_out, Q2Q1_prime_Q0_prime_out, Q2Q1Q0_2_out, Q2Q1Q0_3_out, Q2Q1Q0_4_out,
       Q2Q1Q0_out, Q2Q1Q0_prime_2_out, Q2Q1Q0_prime_3_out, Q2Q1Q0_prime_4_out, Q2Q1Q0_prime_out;

  Clock clock_1 (.out(clock_1_out));
  D_Flip_Flop u_Q2 (.clk(clock_1_out), .D(D2), .Q(Q2));  // open: Qn, preset, en, reset
  D_Flip_Flop u_Q1 (.clk(clock_1_out), .D(D1), .Q(Q1));  // open: Qn, preset, en, reset
  D_Flip_Flop u_Q0 (.clk(clock_1_out), .D(D0), .Q(Q0));  // open: Qn, preset, en, reset
  and Q2_prime_Q1_prime_Q0 (Q2_prime_Q1_prime_Q0_out, ~Q2, ~Q1, ~Q0);  // AND_Gate
  and Q2_prime_Q1_prime_Q0_2 (Q2_prime_Q1_prime_Q0_2_out, ~Q2, ~Q1, Q0);  // AND_Gate
  and Q2_prime_Q1Q0 (Q2_prime_Q1Q0_out, ~Q2, Q1, Q0);  // AND_Gate
  and Q2_prime_Q1Q0_prime (Q2_prime_Q1Q0_prime_out, ~Q2, Q1, ~Q0);  // AND_Gate
  or or_1 (D0, Q2_prime_Q1_prime_Q0_out, Q2_prime_Q1Q0_prime_out, Q2Q1_prime_Q0_prime_2_out, Q2Q1Q0_prime_out);
  and Q2_prime_Q1Q0_prime_2 (Q2_prime_Q1Q0_prime_2_out, ~Q2, Q1, ~Q0);  // AND_Gate
  or or_2 (D1, Q2_prime_Q1_prime_Q0_2_out, Q2_prime_Q1Q0_prime_2_out, Q2Q1_prime_Q0_out, Q2Q1Q0_prime_2_out);
  and Q2Q1_prime_Q0_prime (Q2Q1_prime_Q0_prime_out, Q2, ~Q1, ~Q0);  // AND_Gate
  or or_3 (D2, Q2_prime_Q1Q0_out, Q2Q1_prime_Q0_prime_out, Q2Q1_prime_Q0_prime_3_out, Q2Q1Q0_out);
  and Q2Q1_prime_Q0_prime_2 (Q2Q1_prime_Q0_prime_2_out, Q2, ~Q1, ~Q0);  // AND_Gate
  and Q2Q1Q0_prime (Q2Q1Q0_prime_out, Q2, Q1, ~Q0);  // AND_Gate
  and Q2Q1_prime_Q0 (Q2Q1_prime_Q0_out, Q2, ~Q1, Q0);  // AND_Gate
  and Q2Q1Q0_prime_2 (Q2Q1Q0_prime_2_out, Q2, Q1, ~Q0);  // AND_Gate
  and Q2Q1_prime_Q0_prime_3 (Q2Q1_prime_Q0_prime_3_out, Q2, ~Q1, Q0);  // AND_Gate
  and Q2Q1Q0 (Q2Q1Q0_out, Q2, Q1, ~Q0);  // AND_Gate
  and Q2_prime_Q1_prime_Q0_3 (Q2_prime_Q1_prime_Q0_3_out, ~Q2, ~Q1, Q0);  // AND_Gate
  and Q2_prime_Q1Q0_2 (Q2_prime_Q1Q0_2_out, ~Q2, Q1, Q0);  // AND_Gate
  and Q2_prime_Q1Q0_prime_3 (Q2_prime_Q1Q0_prime_3_out, ~Q2, Q1, ~Q0);  // AND_Gate
  and Q2_prime_Q1Q0_3 (Q2_prime_Q1Q0_3_out, ~Q2, Q1, Q0);  // AND_Gate
  and Q2Q1_prime_Q0_prime_4 (Q2Q1_prime_Q0_prime_4_out, Q2, ~Q1, ~Q0);  // AND_Gate
  and Q2Q1_prime_Q0_2 (Q2Q1_prime_Q0_2_out, Q2, ~Q1, Q0);  // AND_Gate
  and Q2Q1_prime_Q0_3 (Q2Q1_prime_Q0_3_out, Q2, ~Q1, Q0);  // AND_Gate
  or or_4 (S1, Q2_prime_Q1_prime_Q0_3_out, Q2_prime_Q1Q0_2_out, Q2Q1_prime_Q0_3_out, Q2Q1Q0_2_out);
  and Q2Q1Q0_prime_3 (Q2Q1Q0_prime_3_out, Q2, Q1, ~Q0);  // AND_Gate
  or or_5 (S2, Q2_prime_Q1Q0_prime_3_out, Q2_prime_Q1Q0_3_out, Q2Q1Q0_prime_3_out, Q2Q1Q0_3_out);
  and Q2Q1Q0_prime_4 (Q2Q1Q0_prime_4_out, Q2, Q1, ~Q0);  // AND_Gate
  or or_6 (S3, Q2Q1_prime_Q0_prime_4_out, Q2Q1_prime_Q0_2_out, Q2Q1Q0_prime_4_out, Q2Q1Q0_4_out);
  and Q2Q1Q0_2 (Q2Q1Q0_2_out, Q2, Q1, Q0);
  and Q2Q1Q0_3 (Q2Q1Q0_3_out, Q2, Q1, Q0);
  and Q2Q1Q0_4 (Q2Q1Q0_4_out, Q2, Q1, Q0);

  assign S0 = 1'b0;
endmodule

module exMAELEY4 (
  output S3,
  output S2,
  output S1,
  output S0
);

  wire clock_1_out, D0, D1, D2, Q0, Q1, Q2, Q2_prime_Q1_prime_Q0_2_out, Q2_prime_Q1_prime_Q0_3_out,
       Q2_prime_Q1_prime_Q0_out, Q2_prime_Q1Q0_2_out, Q2_prime_Q1Q0_3_out, Q2_prime_Q1Q0_out,
       Q2_prime_Q1Q0_prime_2_out, Q2_prime_Q1Q0_prime_3_out, Q2_prime_Q1Q0_prime_out, Q2Q1_prime_Q0_2_out,
       Q2Q1_prime_Q0_3_out, Q2Q1_prime_Q0_out, Q2Q1_prime_Q0_prime_2_out, Q2Q1_prime_Q0_prime_3_out,
       Q2Q1_prime_Q0_prime_4_out, Q2Q1_prime_Q0_prime_out, Q2Q1Q0_2_out, Q2Q1Q0_3_out, Q2Q1Q0_4_out,
       Q2Q1Q0_out, Q2Q1Q0_prime_2_out, Q2Q1Q0_prime_3_out, Q2Q1Q0_prime_4_out, Q2Q1Q0_prime_out;

  Clock clock_1 (.out(clock_1_out));
  D_Flip_Flop u_Q2 (.clk(clock_1_out), .D(D2), .Q(Q2));  // open: Qn, preset, en, reset
  D_Flip_Flop u_Q1 (.clk(clock_1_out), .D(D1), .Q(Q1));  // open: Qn, preset, en, reset
  D_Flip_Flop u_Q0 (.clk(clock_1_out), .D(D0), .Q(Q0));  // open: Qn, preset, en, reset
  and Q2_prime_Q1_prime_Q0 (Q2_prime_Q1_prime_Q0_out, ~Q2, ~Q1, ~Q0);  // AND_Gate
  and Q2_prime_Q1_prime_Q0_2 (Q2_prime_Q1_prime_Q0_2_out, ~Q2, ~Q1, Q0);  // AND_Gate
  and Q2_prime_Q1Q0 (Q2_prime_Q1Q0_out, ~Q2, Q1, Q0);  // AND_Gate
  and Q2_prime_Q1Q0_prime (Q2_prime_Q1Q0_prime_out, ~Q2, Q1, ~Q0);  // AND_Gate
  or or_1 (D0, Q2_prime_Q1_prime_Q0_out, Q2_prime_Q1Q0_prime_out, Q2Q1_prime_Q0_prime_2_out, Q2Q1Q0_prime_out);
  and Q2_prime_Q1Q0_prime_2 (Q2_prime_Q1Q0_prime_2_out, ~Q2, Q1, ~Q0);  // AND_Gate
  or or_2 (D1, Q2_prime_Q1_prime_Q0_2_out, Q2_prime_Q1Q0_prime_2_out, Q2Q1_prime_Q0_out, Q2Q1Q0_prime_2_out);
  and Q2Q1_prime_Q0_prime (Q2Q1_prime_Q0_prime_out, Q2, ~Q1, ~Q0);  // AND_Gate
  or or_3 (D2, Q2_prime_Q1Q0_out, Q2Q1_prime_Q0_prime_out, Q2Q1_prime_Q0_prime_3_out, Q2Q1Q0_out);
  and Q2Q1_prime_Q0_prime_2 (Q2Q1_prime_Q0_prime_2_out, Q2, ~Q1, ~Q0);  // AND_Gate
  and Q2Q1Q0_prime (Q2Q1Q0_prime_out, Q2, Q1, ~Q0);  // AND_Gate
  and Q2Q1Q0_prime_2 (Q2Q1Q0_prime_2_out, Q2, Q1, ~Q0);  // AND_Gate
  and Q2Q1_prime_Q0 (Q2Q1_prime_Q0_out, Q2, ~Q1, Q0);  // AND_Gate
  and Q2Q1_prime_Q0_prime_3 (Q2Q1_prime_Q0_prime_3_out, Q2, ~Q1, Q0);  // AND_Gate
  and Q2Q1Q0 (Q2Q1Q0_out, Q2, Q1, ~Q0);  // AND_Gate
  and Q2_prime_Q1_prime_Q0_3 (Q2_prime_Q1_prime_Q0_3_out, ~Q2, ~Q1, Q0);  // AND_Gate
  and Q2_prime_Q1Q0_2 (Q2_prime_Q1Q0_2_out, ~Q2, Q1, Q0);  // AND_Gate
  and Q2_prime_Q1Q0_3 (Q2_prime_Q1Q0_3_out, ~Q2, Q1, Q0);  // AND_Gate
  and Q2_prime_Q1Q0_prime_3 (Q2_prime_Q1Q0_prime_3_out, ~Q2, Q1, ~Q0);  // AND_Gate
  and Q2Q1_prime_Q0_prime_4 (Q2Q1_prime_Q0_prime_4_out, Q2, ~Q1, ~Q0);  // AND_Gate
  and Q2Q1_prime_Q0_2 (Q2Q1_prime_Q0_2_out, Q2, ~Q1, Q0);  // AND_Gate
  and Q2Q1_prime_Q0_3 (Q2Q1_prime_Q0_3_out, Q2, ~Q1, Q0);  // AND_Gate
  or or_4 (S1, Q2_prime_Q1_prime_Q0_3_out, Q2_prime_Q1Q0_2_out, Q2Q1_prime_Q0_3_out, Q2Q1Q0_2_out);
  and Q2Q1Q0_prime_3 (Q2Q1Q0_prime_3_out, Q2, Q1, ~Q0);  // AND_Gate
  or or_5 (S2, Q2_prime_Q1Q0_prime_3_out, Q2_prime_Q1Q0_3_out, Q2Q1Q0_prime_3_out, Q2Q1Q0_3_out);
  and Q2Q1Q0_prime_4 (Q2Q1Q0_prime_4_out, Q2, Q1, ~Q0);  // AND_Gate
  or or_6 (S3, Q2Q1_prime_Q0_prime_4_out, Q2Q1_prime_Q0_2_out, Q2Q1Q0_prime_4_out, Q2Q1Q0_4_out);
  and Q2Q1Q0_2 (Q2Q1Q0_2_out, Q2, Q1, Q0);
  and Q2Q1Q0_3 (Q2Q1Q0_3_out, Q2, Q1, Q0);
  and Q2Q1Q0_4 (Q2Q1Q0_4_out, Q2, Q1, Q0);

  assign S0 = 1'b1;
endmodule

module _7segEXSMAELEY (
  input  E,
  input  E_2
);

  wire clock_1_out, display7segmentos_1_dp, display7segmentos_1_sa, display7segmentos_1_sb,
       display7segmentos_1_sc, display7segmentos_1_sd, display7segmentos_1_se, display7segmentos_1_sf,
       display7segmentos_1_sg, display7segmentos_2_dp, display7segmentos_2_sa, display7segmentos_2_sb,
       display7segmentos_2_sc, display7segmentos_2_sd, display7segmentos_2_se, display7segmentos_2_sf,
       display7segmentos_2_sg, display7segmentos_3_dp, display7segmentos_3_sa, display7segmentos_3_sb,
       display7segmentos_3_sc, display7segmentos_3_sd, display7segmentos_3_se, display7segmentos_3_sf,
       display7segmentos_3_sg, display7segmentos_4_dp, display7segmentos_4_sa, display7segmentos_4_sb,
       display7segmentos_4_sc, display7segmentos_4_sd, display7segmentos_4_se, display7segmentos_4_sf,
       display7segmentos_4_sg, EX1_s0, EX1_s1, EX1_s2, EX1_s3, EX2_s0, EX2_s1, EX2_s2, EX2_s3,
       exerciciomealey1_1_s, exmealey2_1_s, IMPARES_s0, IMPARES_s1, IMPARES_s2, IMPARES_s3, PARES_s0,
       PARES_s1, PARES_s2, PARES_s3;

  exercicioMEALEY1 exerciciomealey1_1 (.clock(clock_1_out), .s(exerciciomealey1_1_s), .E(E));
  contador_assincrono EX1 (.in_1(exerciciomealey1_1_s), .s0(EX1_s0), .s1(EX1_s1), .s2(EX1_s2), .s3(EX1_s3));
  exMEALEY2 exmealey2_1 (.S(exmealey2_1_s), .E(E_2));
  contador_assincrono EX2 (.in_1(exmealey2_1_s), .s0(EX2_s0), .s1(EX2_s1), .s2(EX2_s2), .s3(EX2_s3));
  Clock clock_1 (.out(clock_1_out));
  display7segmentos display7segmentos_1 (
    .a(EX1_s3), .b(EX1_s2), .c(EX1_s1), .d(EX1_s0), .sa(display7segmentos_1_sa), .sb(display7segmentos_1_sb),
    .sc(display7segmentos_1_sc), .sd(display7segmentos_1_sd), .se(display7segmentos_1_se),
    .sf(display7segmentos_1_sf), .sg(display7segmentos_1_sg), .dp(display7segmentos_1_dp));
  display7segmentos display7segmentos_2 (
    .a(EX2_s3), .b(EX2_s2), .c(EX2_s1), .d(EX2_s0), .sa(display7segmentos_2_sa), .sb(display7segmentos_2_sb),
    .sc(display7segmentos_2_sc), .sd(display7segmentos_2_sd), .se(display7segmentos_2_se),
    .sf(display7segmentos_2_sf), .sg(display7segmentos_2_sg), .dp(display7segmentos_2_dp));
  _7_Segment_Display u_7_segment_display_1 (
    .g(display7segmentos_1_sg), .f(display7segmentos_1_sf), .a(display7segmentos_1_sa),
    .b(display7segmentos_1_sb), .e(display7segmentos_1_se), .d(display7segmentos_1_sd),
    .c(display7segmentos_1_sc), .dp(display7segmentos_1_dp));
  _7_Segment_Display u_7_segment_display_2 (
    .g(display7segmentos_2_sg), .f(display7segmentos_2_sf), .a(display7segmentos_2_sa),
    .b(display7segmentos_2_sb), .e(display7segmentos_2_se), .d(display7segmentos_2_sd),
    .c(display7segmentos_2_sc), .dp(display7segmentos_2_dp));
  exMEALEY3 IMPARES (.S3(IMPARES_s3), .S2(IMPARES_s2), .S1(IMPARES_s1), .S0(IMPARES_s0));
  exMAELEY4 PARES (.S3(PARES_s3), .S2(PARES_s2), .S1(PARES_s1), .S0(PARES_s0));
  display7segmentos display7segmentos_3 (
    .a(IMPARES_s3), .b(IMPARES_s2), .c(IMPARES_s1), .d(IMPARES_s0), .sa(display7segmentos_3_sa),
    .sb(display7segmentos_3_sb), .sc(display7segmentos_3_sc), .sd(display7segmentos_3_sd),
    .se(display7segmentos_3_se), .sf(display7segmentos_3_sf), .sg(display7segmentos_3_sg),
    .dp(display7segmentos_3_dp));
  display7segmentos display7segmentos_4 (
    .a(PARES_s3), .b(PARES_s2), .c(PARES_s1), .d(PARES_s0), .sa(display7segmentos_4_sa),
    .sb(display7segmentos_4_sb), .sc(display7segmentos_4_sc), .sd(display7segmentos_4_sd),
    .se(display7segmentos_4_se), .sf(display7segmentos_4_sf), .sg(display7segmentos_4_sg),
    .dp(display7segmentos_4_dp));
  _7_Segment_Display u_7_segment_display_3 (
    .g(display7segmentos_3_sg), .f(display7segmentos_3_sf), .a(display7segmentos_3_sa),
    .b(display7segmentos_3_sb), .e(display7segmentos_3_se), .d(display7segmentos_3_sd),
    .c(display7segmentos_3_sc), .dp(display7segmentos_3_dp));
  _7_Segment_Display u_7_segment_display_4 (
    .g(display7segmentos_4_sg), .f(display7segmentos_4_sf), .a(display7segmentos_4_sa),
    .b(display7segmentos_4_sb), .e(display7segmentos_4_se), .d(display7segmentos_4_sd),
    .c(display7segmentos_4_sc), .dp(display7segmentos_4_dp));
endmodule
