// Logisim project 28.09.circ as structural Verilog: 8 circuits, main circuit 2.b
module _2_b (
  input  a,
  input  b,
  input  c,
  input  d,
  output s
);

  wire and_1_out, and_2_out, and_3_out, and_4_out, and_5_out, not_1_out, not_2_out, not_3_out, not_4_out,
       not_5_out, not_6_out, not_7_out, not_8_out;

  not not_1 (not_1_out, b);
  not not_2 (not_2_out, c);
  not not_3 (not_3_out, a);
  not not_4 (not_4_out, b);
  not not_5 (not_5_out, c);
  not not_6 (not_6_out, d);
  not not_7 (not_7_out, a);
  not not_8 (not_8_out, d);
  and and_1 (and_1_out, a, not_1_out, not_2_out, d);
  and and_2 (and_2_out, not_3_out, not_4_out, c, d);
  and and_3 (and_3_out, a, b, not_5_out, not_6_out);
  and and_4 (and_4_out, a, b, c, d);
  and and_5 (and_5_out, not_7_out, b, c, not_8_out);
  or or_1 (s, and_1_out, and_2_out, and_3_out, and_4_out, and_5_out);
endmodule

module _3_b (
  input  a,
  input  b,
  input  c,
  input  d,
  output s
);

  wire and_1_out, and_2_out, and_3_out, and_4_out, not_1_out, not_2_out, not_3_out, not_4_out, not_5_out,
       not_6_out, not_7_out, not_8_out;

  not not_1 (not_1_out, a);
  not not_2 (not_2_out, b);
  not not_3 (not_3_out, d);
  not not_4 (not_4_out, a);
  not not_5 (not_5_out, d);
  not not_6 (not_6_out, b);
  not not_7 (not_7_out, c);
  not not_8 (not_8_out, b);
  and and_1 (and_1_out, not_1_out, not_2_out, c, not_3_out);
  and and_2 (and_2_out, not_4_out, b, c, not_5_out);
  and and_3 (and_3_out, a, not_6_out, not_7_out, d);
  and and_4 (and_4_out, a, not_8_out, c, d);
  or or_1 (s, and_1_out, and_2_out, and_3_out, and_4_out);
endmodule

module _3_d (
  input  a,
  input  b,
  input  c,
  input  d,
  output s
);

  wire and_1_out, and_2_out, not_1_out, not_2_out, not_3_out;

  not not_1 (not_1_out, a);
  and and_1 (and_1_out, not_1_out, c, not_2_out);
  not not_2 (not_2_out, d);
  not not_3 (not_3_out, b);
  and and_2 (and_2_out, a, not_3_out, d);
  or or_1 (s, and_1_out, and_2_out);
endmodule

module _5 (
  input  c,
  input  a,
  input  b,
  output s1,
  output s2
);

  wire and_1_out, and_2_out, xor_1_out;

  and and_1 (and_1_out, a, b);
  xor xor_1 (xor_1_out, b, a);
  and and_2 (and_2_out, xor_1_out, c);
  xor xor_2 (s2, c, xor_1_out);
  or or_1 (s1, and_1_out, and_2_out);
endmodule

module _6_1bit (
  input  a,
  input  b,
  output s
);

  xnor xnor_1 (s, a, b);
endmodule

module _6_2bits (
  input  in_1,
  input  in_2,
  input  in_3,
  input  in_4,
  output out_5
);

  wire n6_1bit_1_s, n6_1bit_2_s;

  _6_1bit u_6_1bit_1 (.a(in_2), .b(in_4), .s(n6_1bit_1_s));
  _6_1bit u_6_1bit_2 (.a(in_1), .b(in_3), .s(n6_1bit_2_s));
  and and_1 (out_5, n6_1bit_1_s, n6_1bit_2_s);

  // Other names for the same wires on the sheet: a0 = in_2; a1 = in_1; b0 = in_4; b1 = in_3
endmodule

module _6_4bits (
  input  in_1,
  input  in_2,
  input  in_3,
  input  in_4,
  input  in_5,
  input  in_6,
  input  in_7,
  input  in_8,
  output out_9
);

  wire n6_2bits_1_out_5, n6_2bits_2_out_5;

  _6_2bits u_6_2bits_1 (.in_1(in_3), .in_3(in_7), .in_2(in_4), .in_4(in_8), .out_5(n6_2bits_1_out_5));
  and and_1 (out_9, n6_2bits_1_out_5, n6_2bits_2_out_5);
  _6_2bits u_6_2bits_2 (.in_1(in_1), .in_3(in_5), .in_2(in_2), .in_4(in_6), .out_5(n6_2bits_2_out_5));

  // Other names for the same wires on the sheet: a0 = in_4; a1 = in_3; a2 = in_2; a3 = in_1; b0 = in_8; b1 = in_7;
  //   b2 = in_6; b3 = in_5
endmodule

module _6_8bits (
  input  in_1,
  input  in_2,
  input  in_3,
  input  in_4,
  input  in_5,
  input  in_6,
  input  in_7,
  input  in_8,
  input  in_9,
  input  in_10,
  input  in_11,
  input  in_12,
  input  in_13,
  input  in_14,
  input  in_15,
  input  in_16,
  output out_17
);

  wire n6_4bits_1_out_9, n6_4bits_2_out_9;

  _6_4bits u_6_4bits_1 (
    .in_1(in_9), .in_5(in_1), .in_2(in_2), .in_6(in_10), .in_3(in_3), .in_7(in_11), .in_4(in_4),
    .in_8(in_12), .out_9(n6_4bits_1_out_9));
  _6_4bits u_6_4bits_2 (
    .in_1(in_13), .in_5(in_5), .in_2(in_6), .in_6(in_14), .in_3(in_7), .in_7(in_15), .in_4(in_8),
    .in_8(in_16), .out_9(n6_4bits_2_out_9));
  and and_1 (out_17, n6_4bits_1_out_9, n6_4bits_2_out_9);

  // Other names for the same wires on the sheet: a0 = in_8; a1 = in_7; a2 = in_6; a3 = in_5; a4 = in_4; a5 = in_3;
  //   a6 = in_2; a7 = in_1; b0 = in_16; b1 = in_15; b2 = in_14; b3 = in_13; b4 = in_12; b5 = in_11; b6 = in_10;
  //   b7 = in_9
endmodule
