// Logisim project atividade_flipflops.circ as structural Verilog: 3 circuits, main circuit flipflops
module flipflops (
  input  in_1,
  input  in_2,
  input  in_3,
  input  in_4,
  input  in_5,
  input  in_6,
  input  in_7,
  input  in_8,
  output out_9,
  output out_10,
  output out_11
);

  wire clock_1_out;

  Clock clock_1 (.out(clock_1_out));
  S_R_Flip_Flop s_r_ff_1 (
    .S(in_4), .clk(clock_1_out), .R(in_5), .Q(out_9), .preset(in_1), .reset(in_3), .en(in_2));  // open: Qn
  D_Flip_Flop d_ff_1 (.clk(clock_1_out), .D(in_6), .Q(out_10), .preset(in_1), .en(in_2), .reset(in_3));  // open: Qn
  J_K_Flip_Flop j_k_ff_1 (
    .J(in_7), .clk(clock_1_out), .K(in_8), .Q(out_11), .preset(in_1), .en(in_2), .reset(in_3));  // open: Qn

  // Other names for the same wires on the sheet: c = in_3; e = in_2; p = in_1
endmodule

module divisor_de_frequencia_8 (
  input  in_1,
  input  in_2,
  input  in_3,
  output out_4,
  output out_5,
  output out_6,
  output out_7,
  output out_8,
  output out_9,
  output out_10,
  output out_11
);

  wire clock_1_out, j_k_ff_1_qn, j_k_ff_2_qn, j_k_ff_3_qn, j_k_ff_4_qn, j_k_ff_5_qn, j_k_ff_6_qn, j_k_ff_7_qn;

  Clock clock_1 (.out(clock_1_out));
  J_K_Flip_Flop j_k_ff_1 (
    .J(1'b1), .clk(clock_1_out), .K(1'b1), .Q(out_4), .Qn(j_k_ff_1_qn), .preset(in_1), .en(in_2), .reset(in_3));
  J_K_Flip_Flop j_k_ff_2 (
    .J(1'b1), .clk(j_k_ff_1_qn), .K(1'b1), .Q(out_5), .Qn(j_k_ff_2_qn), .preset(in_1), .en(in_2), .reset(in_3));
  J_K_Flip_Flop j_k_ff_3 (
    .J(1'b1), .clk(j_k_ff_2_qn), .K(1'b1), .Q(out_6), .Qn(j_k_ff_3_qn), .preset(in_1), .en(in_2), .reset(in_3));
  J_K_Flip_Flop j_k_ff_4 (
    .J(1'b1), .clk(j_k_ff_3_qn), .K(1'b1), .Q(out_7), .Qn(j_k_ff_4_qn), .preset(in_1), .en(in_2), .reset(in_3));
  J_K_Flip_Flop j_k_ff_5 (
    .J(1'b1), .clk(j_k_ff_4_qn), .K(1'b1), .Q(out_8), .Qn(j_k_ff_5_qn), .preset(in_1), .en(in_2), .reset(in_3));
  J_K_Flip_Flop j_k_ff_6 (
    .J(1'b1), .clk(j_k_ff_5_qn), .K(1'b1), .Q(out_9), .Qn(j_k_ff_6_qn), .preset(in_1), .en(in_2), .reset(in_3));
  J_K_Flip_Flop j_k_ff_7 (
    .J(1'b1), .clk(j_k_ff_6_qn), .K(1'b1), .Q(out_10), .Qn(j_k_ff_7_qn), .preset(in_1), .en(in_2),
    .reset(in_3));
  J_K_Flip_Flop j_k_ff_8 (
    .J(1'b1), .clk(j_k_ff_7_qn), .K(1'b1), .Q(out_11), .preset(in_1), .en(in_2), .reset(in_3));  // open: Qn

  // Other names for the same wires on the sheet: c = in_3; e = in_2; p = in_1
endmodule

module registrador_de_deslocamento (
  input  in_1,
  input  in_2,
  input  in_3,
  input  in_4,
  output out_5,
  output out_6,
  output out_7,
  output out_8,
  output out_9,
  output out_10,
  output out_11,
  output out_12
);

  wire clock_1_out, j_k_ff_1_qn, j_k_ff_2_qn, j_k_ff_3_qn, j_k_ff_4_qn, j_k_ff_5_qn, j_k_ff_6_qn,
       j_k_ff_7_qn, not_1_out;

  Clock clock_1 (.out(clock_1_out));
  not not_1 (not_1_out, in_4);
  J_K_Flip_Flop j_k_ff_1 (
    .J(in_4), .clk(clock_1_out), .K(not_1_out), .Q(out_5), .Qn(j_k_ff_1_qn), .preset(in_1), .en(in_2),
    .reset(in_3));
  J_K_Flip_Flop j_k_ff_2 (
    .J(out_5), .clk(clock_1_out), .K(j_k_ff_1_qn), .Q(out_6), .Qn(j_k_ff_2_qn), .preset(in_1), .en(in_2),
    .reset(in_3));
  J_K_Flip_Flop j_k_ff_3 (
    .J(out_6), .clk(clock_1_out), .K(j_k_ff_2_qn), .Q(out_7), .Qn(j_k_ff_3_qn), .preset(in_1), .en(in_2),
    .reset(in_3));
  J_K_Flip_Flop j_k_ff_4 (
    .J(out_7), .clk(clock_1_out), .K(j_k_ff_3_qn), .Q(out_8), .Qn(j_k_ff_4_qn), .preset(in_1), .en(in_2),
    .reset(in_3));
  J_K_Flip_Flop j_k_ff_5 (
    .J(out_8), .clk(clock_1_out), .K(j_k_ff_4_qn), .Q(out_9), .Qn(j_k_ff_5_qn), .preset(in_1), .en(in_2),
    .reset(in_3));
  J_K_Flip_Flop j_k_ff_6 (
    .J(out_9), .clk(clock_1_out), .K(j_k_ff_5_qn), .Q(out_10), .Qn(j_k_ff_6_qn), .preset(in_1), .en(in_2),
    .reset(in_3));
  J_K_Flip_Flop j_k_ff_7 (
    .J(out_10), .clk(clock_1_out), .K(j_k_ff_6_qn), .Q(out_11), .Qn(j_k_ff_7_qn), .preset(in_1), .en(in_2),
    .reset(in_3));
  J_K_Flip_Flop j_k_ff_8 (
    .J(out_11), .clk(clock_1_out), .K(j_k_ff_7_qn), .Q(out_12), .preset(in_1), .en(in_2), .reset(in_3));  // open: Qn

  // Other names for the same wires on the sheet: c = in_3; e = in_2; p = in_1
endmodule
