// Logisim project projetoSistemasDigitais.circ as structural Verilog: 15 circuits, main circuit main
module main (
  output [8:0] out_1
);

  wire _0_5_out, _1_out, fsm_moore_1_saida, or_1_out, s_r_ff_1_q;
  wire [3:0] C1, C1_2;
  wire [12:9] contador_moeda_1_saida;

  FSM_Moore fsm_moore_1 (.CLOCK(or_1_out), .ENTRADA(s_r_ff_1_q), .SAIDA(fsm_moore_1_saida));
  or or_1 (or_1_out, _0_5_out, _1_out);
  Button _0_5 (.out(_0_5_out));
  Button _1 (.out(_1_out));
  S_R_Flip_Flop s_r_ff_1 (.S(_1_out), .clk(or_1_out), .R(_0_5_out), .Q(s_r_ff_1_q));  // open: Qn, preset, reset, en
  contador_moeda contador_moeda_1 (._50C(_0_5_out), ._1R(_1_out), .saida({contador_moeda_1_saida, out_1}));
  contador_assinc_decada contador_assinc_decada_1 (
    .CLOCK(fsm_moore_1_saida), .s0(C1[0]), .s1(C1[1]), .s2(C1[2]), .s3(C1[3]), .s4(C1_2[0]), .s5(C1_2[1]),
    .s6(C1_2[2]), .s7(C1_2[3]));
  Hex_Digit_Display hex_digit_display_1 (.value(C1));  // open: dp
  Hex_Digit_Display hex_digit_display_2 (.value(C1_2));  // open: dp
  // Pins of 9 and 13 bits meet at {contador_moeda_1_saida, out_1}
endmodule

module circuito_Moore (
  input  Q0,
  input  Q1,
  input  E,
  output D0,
  output D1,
  output S
);

  wire and_1_out, and_2_out, and_3_out, and_4_out, and_5_out, and_6_out, not_1_out, not_2_out, not_3_out,
       not_4_out, not_5_out, not_6_out, not_7_out;

  not not_1 (not_1_out, Q0);
  not not_2 (not_2_out, E);
  not not_3 (not_3_out, Q0);
  not not_4 (not_4_out, Q1);
  not not_5 (not_5_out, E);
  not not_6 (not_6_out, Q1);
  not not_7 (not_7_out, Q0);
  and and_1 (and_1_out, not_1_out, not_2_out);
  and and_2 (and_2_out, not_3_out, Q1);
  and and_3 (and_3_out, Q0, not_4_out, E);
  and and_4 (and_4_out, Q0, Q1, not_5_out);
  and and_5 (and_5_out, Q0, not_6_out);
  and and_6 (and_6_out, not_7_out, Q1);
  and and_7 (S, Q0, Q1);
  or u_D0 (D0, and_1_out, and_2_out, and_3_out, and_4_out);
  or u_D1 (D1, E, and_5_out, and_6_out);
endmodule

module FSM_Moore (
  input  CLOCK,
  input  ENTRADA,
  output SAIDA
);

  wire Circuito_d0, Circuito_d1, D0_q, D1_q;

  D_Flip_Flop D1 (.clk(CLOCK), .D(Circuito_d1), .Q(D1_q));  // open: Qn, preset, en, reset
  circuito_Moore Circuito (.Q0(D0_q), .Q1(D1_q), .E(ENTRADA), .D0(Circuito_d0), .D1(Circuito_d1), .S(SAIDA));
  D_Flip_Flop D0 (.clk(CLOCK), .D(Circuito_d0), .Q(D0_q));  // open: Qn, preset, en, reset

  // Other names for the same wires on the sheet: ck = CLOCK; E = ENTRADA; S = SAIDA
endmodule

module contador_moeda (
  input  _50C,
  input  _1R,
  output [12:0] saida
);

  wire and_1_out, contador_1bit_1_out, or_1_out;

  contador_1BIT contador_1bit_1 (.CLOCK(_50C), .s0(saida[0]), .OUT(contador_1bit_1_out));
  and and_1 (and_1_out, _50C, contador_1bit_1_out);
  or or_1 (or_1_out, _1R, and_1_out);
  contador0_999 contador0_999_1 (
    .CLOCK(or_1_out), .s0(saida[1]), .s1(saida[2]), .s2(saida[3]), .s3(saida[4]), .s4(saida[5]),
    .s5(saida[6]), .s6(saida[7]), .s7(saida[8]), .s8(saida[9]), .s9(saida[10]), .s10(saida[11]),
    .s11(saida[12]));

  // Other names for the same wires on the sheet: _1REAL = _1R; _50CENTAVOS = _50C; LSB = saida[0]
endmodule

module somador9bits (
  input  LSB_A,
  input  LSB_B,
  input  [7:0] A_8BITS,
  input  [7:0] B_8BITS,
  output [9:0] SAIDA_10BITS
);

  wire O0;

  somador8bits somador8bits_1 (
    .A7(A_8BITS[7]), .B7(B_8BITS[7]), .A6(A_8BITS[6]), .B6(B_8BITS[6]), .A5(A_8BITS[5]), .B5(B_8BITS[5]),
    .A4(A_8BITS[4]), .B4(B_8BITS[4]), .A3(A_8BITS[3]), .B3(B_8BITS[3]), .A2(A_8BITS[2]), .B2(B_8BITS[2]),
    .A1(A_8BITS[1]), .B1(B_8BITS[1]), .A0(A_8BITS[0]), .B0(B_8BITS[0]), .CIN0(O0),
    .SAIDAS4_8(SAIDA_10BITS[9:5]), .SAIDAS0_3(SAIDA_10BITS[4:1]));
  Ha ha_1 (.A(LSB_B), .B(LSB_A), .Cout(O0), .S(SAIDA_10BITS[0]));

  // Other names for the same wires on the sheet: A0 = A_8BITS[0]; A1 = A_8BITS[1]; A2 = A_8BITS[2]; A3 = A_8BITS[3];
  //   A4 = A_8BITS[4]; A5 = A_8BITS[5]; A6 = A_8BITS[6]; A7 = A_8BITS[7]; B0 = B_8BITS[0]; B1 = B_8BITS[1];
  //   B2 = B_8BITS[2]; B3 = B_8BITS[3]; B4 = B_8BITS[4]; B5 = B_8BITS[5]; B6 = B_8BITS[6]; B7 = B_8BITS[7];
  //   S0 = SAIDA_10BITS[0]; SAIDA[9:0] = SAIDA_10BITS
endmodule

module somador4bits (
  input  A3,
  input  A2,
  input  A1,
  input  A0,
  input  B3,
  input  B2,
  input  B1,
  input  B0,
  input  CIN0,
  output S4,
  output S3,
  output S2,
  output S1,
  output S0
);

  wire O0, O1, O2;

  FA fa_1 (.A(A3), .B(B3), .Cin(O2), .Cout(S4), .S(S3));
  FA fa_2 (.A(A2), .B(B2), .Cin(O1), .Cout(O2), .S(S2));
  FA fa_3 (.A(A0), .B(B0), .Cin(CIN0), .Cout(O0), .S(S0));
  FA fa_4 (.A(A1), .B(B1), .Cin(O0), .Cout(O1), .S(S1));
endmodule

module somador8bits (
  input  A7,
  input  A6,
  input  A5,
  input  A4,
  input  A3,
  input  A2,
  input  A1,
  input  A0,
  input  B7,
  input  B6,
  input  B5,
  input  B4,
  input  B3,
  input  B2,
  input  B1,
  input  B0,
  input  CIN0,
  output [4:0] SAIDAS4_8,
  output [3:0] SAIDAS0_3
);

  wire O4;

  somador4bits somador4bits_1 (
    .A3(A7), .B3(B7), .A2(A6), .B2(B6), .A1(A5), .B1(B5), .A0(A4), .B0(B4), .S4(SAIDAS4_8[4]),
    .S3(SAIDAS4_8[3]), .S2(SAIDAS4_8[2]), .S1(SAIDAS4_8[1]), .S0(SAIDAS4_8[0]), .CIN0(O4));
  somador4bits somador4bits_2 (
    .A3(A3), .B3(B3), .A2(A2), .B2(B2), .A1(A1), .B1(B1), .A0(A0), .B0(B0), .S4(O4), .S3(SAIDAS0_3[3]),
    .S2(SAIDAS0_3[2]), .S1(SAIDAS0_3[1]), .S0(SAIDAS0_3[0]), .CIN0(CIN0));
endmodule

module contador_1BIT (
  input  CLOCK,
  output s0,
  output OUT
);

  wire not_1_out;

  not not_1 (not_1_out, CLOCK);
  J_K_Flip_Flop j_k_ff_1 (.J(1'b1), .clk(not_1_out), .K(1'b1), .Q(OUT), .en(1'b1));  // open: Qn, preset, reset

  assign s0 = OUT;
endmodule

module Circuito_Maeley (
  input  Q0,
  input  Q1,
  input  E,
  output D0,
  output D1,
  output S
);

  wire and_1_out, and_2_out, and_3_out, and_4_out, and_5_out, and_6_out, and_7_out, and_8_out, and_9_out,
       not_1_out, not_2_out, not_3_out, not_4_out, not_5_out, not_6_out, not_7_out, not_8_out, not_9_out,
       not_10_out, not_11_out;

  not not_1 (not_1_out, Q0);
  not not_2 (not_2_out, E);
  not not_3 (not_3_out, Q0);
  not not_4 (not_4_out, Q1);
  not not_5 (not_5_out, E);
  not not_6 (not_6_out, Q1);
  not not_7 (not_7_out, Q0);
  not not_8 (not_8_out, Q1);
  not not_9 (not_9_out, Q0);
  not not_10 (not_10_out, Q0);
  not not_11 (not_11_out, E);
  and and_1 (and_1_out, not_1_out, not_2_out);
  and and_2 (and_2_out, not_3_out, Q1);
  and and_3 (and_3_out, Q0, not_4_out, E);
  and and_4 (and_4_out, Q0, Q1, not_5_out);
  and and_5 (and_5_out, Q0, not_6_out);
  and and_6 (and_6_out, not_7_out, Q1);
  and and_7 (and_7_out, not_8_out, E, Q0);
  and and_8 (and_8_out, Q1, not_9_out, E);
  and and_9 (and_9_out, Q1, not_10_out, not_11_out);
  or u_D0 (D0, and_1_out, and_2_out, and_3_out, and_4_out);
  or u_D1 (D1, E, and_5_out, and_6_out);
  or u_S (S, and_7_out, and_8_out, and_9_out);
endmodule

module TESTE (
);

  wire _1_REAL_out, _50_CENT_out, and_1_out, and_2_out, button_1_out, FSM_saida, latchrs_1_q, latchrs_2_q,
       latchrs_2_q_prime, or_1_out, or_2_out;
  wire [0:0] CONTADOR_DINHEIRO_saida;
  wire [3:0] _1, _2, _3, C1, C1_2, converte1_5_1_out_2, SAIDA_a, SAIDA_c, SAIDA_e, SAIDA_f;

  Button button_1 (.out(button_1_out));
  FSM_Moore FSM (.CLOCK(button_1_out), .ENTRADA(latchrs_1_q), .SAIDA(FSM_saida));
  latchRS latchrs_1 (.R(_1_REAL_out), .C(or_1_out), .Q(latchrs_1_q));  // open: Q_prime
  or or_1 (or_1_out, _1_REAL_out, _50_CENT_out);
  Button _1_REAL (.out(_1_REAL_out));
  Button _50_CENT (.out(_50_CENT_out));
  contadorBordaPositiva CONTADOR_CAFE (
    .CLOCK(FSM_saida), .s0(C1[0]), .s1(C1[1]), .s2(C1[2]), .s3(C1[3]), .s4(C1_2[0]), .s5(C1_2[1]),
    .s6(C1_2[2]), .s7(C1_2[3]));
  or or_2 (or_2_out, _50_CENT_out, _1_REAL_out);
  Hex_Digit_Display hex_digit_display_1 (.value(C1));  // open: dp
  Hex_Digit_Display hex_digit_display_2 (.value(C1_2));  // open: dp
  latchRS latchrs_2 (.R(_1_REAL_out), .C(or_2_out), .Q(latchrs_2_q), .Q_prime(latchrs_2_q_prime));
  and and_1 (and_1_out, button_1_out, ~latchrs_2_q);  // AND_Gate
  contador_moeda CONTADOR_DINHEIRO (
    ._50C(and_1_out), ._1R(and_2_out), .saida({_3, _2, _1, CONTADOR_DINHEIRO_saida[0]}));
  and and_2 (and_2_out, ~latchrs_2_q_prime, button_1_out);  // AND_Gate
  Hex_Digit_Display hex_digit_display_3 (.value(SAIDA_a));  // open: dp
  Hex_Digit_Display hex_digit_display_4 (.value(SAIDA_c));  // open: dp
  Hex_Digit_Display hex_digit_display_5 (.value(SAIDA_e));  // open: dp
  Hex_Digit_Display hex_digit_display_6 (.value(SAIDA_f));  // open: dp
  _0xCAFE SAIDA (.ENTRADA(FSM_saida), .C(SAIDA_c), .A(SAIDA_a), .F(SAIDA_f), .E(SAIDA_e));
  Hex_Digit_Display hex_digit_display_7 (.value(_3));  // open: dp
  Hex_Digit_Display hex_digit_display_8 (.value(_2));  // open: dp
  Hex_Digit_Display hex_digit_display_9 (.value(_1), .dp(1'b1));
  Hex_Digit_Display hex_digit_display_10 (.value(converte1_5_1_out_2));  // open: dp
  converte1_5 converte1_5_1 (.ENTRADA(CONTADOR_DINHEIRO_saida[0]), .out_2(converte1_5_1_out_2));
endmodule

module FSM_Maeley (
  input  CLOCK,
  input  ENTRADA,
  output SAIDA
);

  wire circuito_maeley_1_d0, circuito_maeley_1_d1, D0_q, D1_q;

  D_Flip_Flop D1 (.clk(CLOCK), .D(circuito_maeley_1_d1), .Q(D1_q));  // open: Qn, preset, en, reset
  Circuito_Maeley circuito_maeley_1 (
    .Q0(D0_q), .Q1(D1_q), .E(ENTRADA), .D0(circuito_maeley_1_d0), .D1(circuito_maeley_1_d1), .S(SAIDA));
  D_Flip_Flop D0 (.clk(CLOCK), .D(circuito_maeley_1_d0), .Q(D0_q));  // open: Qn, preset, en, reset

  // Other names for the same wires on the sheet: ck = CLOCK; E = ENTRADA; S = SAIDA
endmodule

module contador0_999 (
  input  CLOCK,
  output s1,
  output s5,
  output s2,
  output s9,
  output s0,
  output s6,
  output s4,
  output s10,
  output s3,
  output s8,
  output s7,
  output s11
);

  wire and_1_out, and_2_out, and_3_out, j_k_ff_1_qn, j_k_ff_3_qn, j_k_ff_5_qn, j_k_ff_7_qn, j_k_ff_9_qn,
       j_k_ff_11_qn, not_1_out, not_2_out, not_3_out, not_4_out, not_5_out, not_6_out, not_7_out, not_8_out,
       not_9_out, not_10_out, not_11_out, not_12_out, not_13_out, not_14_out, not_15_out, not_16_out,
       not_17_out, not_18_out;

  not not_1 (not_1_out, CLOCK);
  J_K_Flip_Flop j_k_ff_1 (
    .J(1'b1), .clk(not_1_out), .K(1'b1), .Q(s0), .Qn(j_k_ff_1_qn), .preset(1'b0), .en(1'b1), .reset(not_5_out));
  not not_2 (not_2_out, s0);
  J_K_Flip_Flop j_k_ff_2 (
    .J(1'b1), .clk(not_2_out), .K(1'b1), .Q(s1), .preset(1'b0), .en(1'b1), .reset(not_5_out));  // open: Qn
  J_K_Flip_Flop j_k_ff_3 (
    .J(1'b1), .clk(not_3_out), .K(1'b1), .Q(s2), .Qn(j_k_ff_3_qn), .preset(1'b0), .en(1'b1), .reset(not_5_out));
  not not_3 (not_3_out, s1);
  not not_4 (not_4_out, s2);
  J_K_Flip_Flop j_k_ff_4 (
    .J(1'b1), .clk(not_4_out), .K(1'b1), .Q(s3), .preset(1'b0), .en(1'b1), .reset(not_5_out));  // open: Qn
  and and_1 (and_1_out, s3, s1, j_k_ff_3_qn, j_k_ff_1_qn);
  not not_5 (not_5_out, not_6_out);
  not not_6 (not_6_out, and_1_out);
  not not_7 (not_7_out, not_5_out);
  J_K_Flip_Flop j_k_ff_5 (
    .J(1'b1), .clk(not_7_out), .K(1'b1), .Q(s4), .Qn(j_k_ff_5_qn), .preset(1'b0), .en(1'b1),
    .reset(not_11_out));
  not not_8 (not_8_out, s4);
  J_K_Flip_Flop j_k_ff_6 (
    .J(1'b1), .clk(not_8_out), .K(1'b1), .Q(s5), .preset(1'b0), .en(1'b1), .reset(not_11_out));  // open: Qn
  not not_9 (not_9_out, s5);
  J_K_Flip_Flop j_k_ff_7 (
    .J(1'b1), .clk(not_9_out), .K(1'b1), .Q(s6), .Qn(j_k_ff_7_qn), .preset(1'b0), .en(1'b1),
    .reset(not_11_out));
  not not_10 (not_10_out, s6);
  J_K_Flip_Flop j_k_ff_8 (
    .J(1'b1), .clk(not_10_out), .K(1'b1), .Q(s7), .preset(1'b0), .en(1'b1), .reset(not_11_out));  // open: Qn
  and and_2 (and_2_out, s7, s5, j_k_ff_7_qn, j_k_ff_5_qn);
  not not_11 (not_11_out, not_12_out);
  not not_12 (not_12_out, and_2_out);
  not not_13 (not_13_out, not_11_out);
  J_K_Flip_Flop j_k_ff_9 (
    .J(1'b1), .clk(not_13_out), .K(1'b1), .Q(s8), .Qn(j_k_ff_9_qn), .preset(1'b0), .en(1'b1),
    .reset(not_17_out));
  not not_14 (not_14_out, s8);
  J_K_Flip_Flop j_k_ff_10 (
    .J(1'b1), .clk(not_14_out), .K(1'b1), .Q(s9), .preset(1'b0), .en(1'b1), .reset(not_17_out));  // open: Qn
  not not_15 (not_15_out, s9);
  not not_16 (not_16_out, s10);
  J_K_Flip_Flop j_k_ff_11 (
    .J(1'b1), .clk(not_15_out), .K(1'b1), .Q(s10), .Qn(j_k_ff_11_qn), .preset(1'b0), .en(1'b1),
    .reset(not_17_out));
  J_K_Flip_Flop j_k_ff_12 (
    .J(1'b1), .clk(not_16_out), .K(1'b1), .Q(s11), .preset(1'b0), .en(1'b1), .reset(not_17_out));  // open: Qn
  not not_17 (not_17_out, not_18_out);
  not not_18 (not_18_out, and_3_out);
  and and_3 (and_3_out, s11, s9, j_k_ff_11_qn, j_k_ff_9_qn);
endmodule

module converte1_5 (
  input  ENTRADA,
  output [3:0] out_2
);


  assign out_2 = {1'b0, ENTRADA, 1'b0, ENTRADA};
endmodule

module _0xCAFE (
  input  ENTRADA,
  output [3:0] C,
  output [3:0] A,
  output [3:0] F,
  output [3:0] E
);


  assign A = {ENTRADA, 1'b0, ENTRADA, 1'b0};
  assign C = {{2{ENTRADA}}, 2'b00};
  assign E = {{3{ENTRADA}}, 1'b0};
  assign F = {4{ENTRADA}};
endmodule

module contadorBordaPositiva (
  input  CLOCK,
  output s1,
  output s2,
  output s5,
  output s0,
  output s6,
  output s3,
  output s4,
  output s7
);

  wire and_1_out, and_2_out, j_k_ff_1_qn, j_k_ff_3_qn, j_k_ff_5_qn, j_k_ff_7_qn, not_1_out, not_2_out,
       not_3_out, not_4_out, not_5_out, not_6_out, not_7_out, not_8_out, not_9_out, not_10_out, not_11_out;

  J_K_Flip_Flop j_k_ff_1 (
    .J(1'b1), .clk(CLOCK), .K(1'b1), .Q(s0), .Qn(j_k_ff_1_qn), .preset(1'b0), .en(1'b1), .reset(not_4_out));
  not not_1 (not_1_out, s0);
  J_K_Flip_Flop j_k_ff_2 (
    .J(1'b1), .clk(not_1_out), .K(1'b1), .Q(s1), .preset(1'b0), .en(1'b1), .reset(not_4_out));  // open: Qn
  not not_2 (not_2_out, s1);
  J_K_Flip_Flop j_k_ff_3 (
    .J(1'b1), .clk(not_2_out), .K(1'b1), .Q(s2), .Qn(j_k_ff_3_qn), .preset(1'b0), .en(1'b1), .reset(not_4_out));
  not not_3 (not_3_out, s2);
  J_K_Flip_Flop j_k_ff_4 (
    .J(1'b1), .clk(not_3_out), .K(1'b1), .Q(s3), .preset(1'b0), .en(1'b1), .reset(not_4_out));  // open: Qn
  and and_1 (and_1_out, s3, s1, j_k_ff_3_qn, j_k_ff_1_qn);
  not not_4 (not_4_out, not_5_out);
  not not_5 (not_5_out, and_1_out);
  not not_6 (not_6_out, not_4_out);
  J_K_Flip_Flop j_k_ff_5 (
    .J(1'b1), .clk(not_6_out), .K(1'b1), .Q(s4), .Qn(j_k_ff_5_qn), .preset(1'b0), .en(1'b1),
    .reset(not_10_out));
  not not_7 (not_7_out, s4);
  J_K_Flip_Flop j_k_ff_6 (
    .J(1'b1), .clk(not_7_out), .K(1'b1), .Q(s5), .preset(1'b0), .en(1'b1), .reset(not_10_out));  // open: Qn
  not not_8 (not_8_out, s5);
  J_K_Flip_Flop j_k_ff_7 (
    .J(1'b1), .clk(not_8_out), .K(1'b1), .Q(s6), .Qn(j_k_ff_7_qn), .preset(1'b0), .en(1'b1),
    .reset(not_10_out));
  not not_9 (not_9_out, s6);
  J_K_Flip_Flop j_k_ff_8 (
    .J(1'b1), .clk(not_9_out), .K(1'b1), .Q(s7), .preset(1'b0), .en(1'b1), .reset(not_10_out));  // open: Qn
  and and_2 (and_2_out, s7, s5, j_k_ff_7_qn, j_k_ff_5_qn);
  not not_10 (not_10_out, not_11_out);
  not not_11 (not_11_out, and_2_out);
endmodule
